// Logisim project iochip.circ as structural Verilog: 4 circuits, main circuit main
module main (
  input  C5i,
  input  A6i,
  input  B0i,
  input  B2i,
  input  in_5,
  input  A4i,
  input  w2,
  input  A5i,
  input  in_9,
  input  in_10,
  input  TEST,
  input  SRES,
  input  VCLK,
  input  PAL,
  output C4o,
  output out_16
);

  wire and_1_out, and_2_out, and_3_out, and_4_out, and_5_out, and_6_out, and_7_out, and_8_out, and_9_out,
       and_10_out, and_11_out, and_12_out, and_13_out, and_14_out, and_15_out, and_16_out, buffer_2_out,
       buffer_3_out, clk_div_1_out_4, d_ff_1_q, d_ff_1_qn, d_ff_4_q, d_ff_5_q, d_ff_6_q, d_ff_7_q, d_ff_8_q,
       d_ff_8_qn, d_ff_9_q, d_ff_9_qn, d_ff_10_qn, d_ff_11_qn, d_ff_12_qn, d_ff_13_qn, d_ff_14_qn,
       d_ff_15_qn, d_ff_16_qn, d_ff_17_qn, d_ff_18_q, d_ff_18_qn, d_ff_19_q, d_ff_19_qn, d_ff_20_q,
       d_ff_20_qn, d_ff_21_q, d_ff_21_qn, d_ff_22_q, d_ff_23_q, d_ff_24_q, d_ff_25_q, d_ff_26_q, d_ff_27_q,
       d_ff_28_q, d_ff_29_q, d_ff_30_q, d_ff_30_qn, d_ff_31_q, d_ff_31_qn, d_ff_32_q, d_ff_32_qn, d_ff_33_qn,
       d_ff_34_q, d_ff_34_qn, d_ff_35_q, d_ff_36_q, d_ff_36_qn, d_ff_37_q, d_ff_37_qn, d_ff_38_q, d_ff_38_qn,
       d_ff_39_q, d_ff_39_qn, d_ff_40_q, d_ff_40_qn, d_ff_41_q, d_ff_42_q, d_ff_43_q, d_ff_43_qn, d_ff_44_q,
       d_ff_45_q, d_ff_45_qn, d_ff_46_q, d_ff_47_q, d_ff_47_qn, d_ff_50_q, d_ff_53_q, d_ff_55_q, d_ff_56_q,
       d_ff_56_qn, d_ff_58_q, d_ff_59_q, d_ff_59_qn, d_ff_61_q, d_ff_63_q, d_ff_64_q, d_ff_64_qn, d_ff_66_q,
       d_ff_67_q, d_ff_67_qn, d_ff_69_q, multiplexer_6_out, multiplexer_7_out, multiplexer_8_out,
       multiplexer_9_out, multiplexer_10_out, multiplexer_11_out, multiplexer_12_out, multiplexer_13_out,
       multiplexer_14_out, nand_1_out, nand_2_out, nand_3_out, nand_4_out, nand_5_out, nand_6_out,
       nand_7_out, nand_8_out, nand_9_out, nand_10_out, nand_11_out, nand_12_out, nand_13_out, nand_14_out,
       nand_15_out, nand_16_out, nand_17_out, nand_18_out, nand_19_out, nand_20_out, nand_21_out,
       nand_22_out, nand_23_out, nand_24_out, nand_25_out, nand_26_out, nand_27_out, nand_28_out,
       nand_29_out, nand_30_out, nand_31_out, nand_32_out, nand_33_out, nand_34_out, nand_35_out,
       nand_36_out, nand_37_out, nand_38_out, nand_39_out, nand_40_out, nand_41_out, nor_1_out, nor_2_out,
       nor_3_out, not_1_out, not_2_out, not_3_out, not_4_out, not_5_out, not_6_out, not_7_out, not_8_out,
       not_9_out, not_10_out, not_11_out, not_12_out, not_13_out, not_14_out, not_15_out, not_16_out,
       not_17_out, not_18_out, not_19_out, not_20_out, not_21_out, not_22_out, not_23_out, not_24_out,
       not_25_out, not_26_out, not_27_out, not_28_out, not_29_out, not_30_out, not_31_out, not_32_out,
       not_33_out, not_34_out, not_35_out, or_1_out, or_2_out, or_3_out, or_4_out, or_5_out, or_6_out,
       or_7_out, undriven, undriven_3, undriven_4, undriven_5, undriven_6, undriven_7, xor_delay_6x_1_out_2,
       xor_delay_6x_2_out_2, xor_delay_6x_3_out_2, xor_delay_6x_4_out_2, xor_delay_6x_5_out_2,
       xor_delay_6x_6_out_2, xor_delay_6x_7_out_2, xor_delay_6x_8_out_2;
  wire [7:0] d_ff_68_q, undriven_2;

  Multiplexer multiplexer_1 (.in0(B0i), .in1(A6i), .sel(w2));  // open: out
  Multiplexer multiplexer_2 (.in0(A4i), .in1(A4i), .sel(w2));  // open: out
  buf and_1 (and_1_out, A5i);  // AND_Gate
  not not_1 (not_1_out, in_10);
  D_Flip_Flop d_ff_1 (.D(SRES), .clk(VCLK), .Q(d_ff_1_q), .Qn(d_ff_1_qn));  // open: preset, reset
  not not_2 (not_2_out, PAL);
  Multiplexer multiplexer_3 (.in0(B2i), .in1(in_5), .sel(w2));  // open: out
  D_Flip_Flop d_ff_2 (.D(undriven_2[2]), .clk(undriven), .reset(not_3_out));  // open: Q, Qn, preset
  D_Flip_Flop d_ff_3 (.D(undriven_2[3]), .clk(undriven), .reset(not_3_out));  // open: Q, Qn, preset
  D_Flip_Flop d_ff_4 (.D(undriven_2[4]), .clk(undriven), .Q(d_ff_4_q), .reset(not_3_out));  // open: Qn, preset
  D_Flip_Flop d_ff_5 (.D(undriven_2[5]), .clk(undriven), .Q(d_ff_5_q), .reset(not_3_out));  // open: Qn, preset
  D_Flip_Flop d_ff_6 (.D(undriven_2[6]), .clk(undriven), .Q(d_ff_6_q), .reset(not_3_out));  // open: Qn, preset
  D_Flip_Flop d_ff_7 (.D(undriven_2[7]), .clk(undriven), .Q(d_ff_7_q), .reset(not_3_out));  // open: Qn, preset
  not not_3 (not_3_out, in_9);
  not not_4 (not_4_out, multiplexer_14_out);
  not not_5 (not_5_out, d_ff_31_q);
  Multiplexer multiplexer_4 (.in0(and_1_out), .in1(A5i), .sel(w2));  // open: out
  D_Flip_Flop d_ff_8 (.D(d_ff_8_qn), .clk(not_4_out), .Q(d_ff_8_q), .Qn(d_ff_8_qn), .reset(not_1_out));  // open: preset
  D_Flip_Flop d_ff_9 (.D(d_ff_9_qn), .clk(not_5_out), .Q(d_ff_9_q), .Qn(d_ff_9_qn), .reset(not_1_out));  // open: preset
  buf buffer_1 (out_16, d_ff_1_qn);
  not not_6 (not_6_out, d_ff_6_q);
  buf buffer_2 (buffer_2_out, d_ff_6_q);
  not not_7 (not_7_out, d_ff_7_q);
  buf buffer_3 (buffer_3_out, d_ff_7_q);
  not not_8 (not_8_out, d_ff_8_q);
  not not_9 (not_9_out, d_ff_9_q);
  D_Flip_Flop #(.trigger("high")) d_ff_10 (
    .D(undriven_2[0]), .clk(undriven_3), .Qn(d_ff_10_qn));  // open: Q, preset, reset
  D_Flip_Flop #(.trigger("high")) d_ff_11 (
    .D(undriven_2[1]), .clk(undriven_3), .Qn(d_ff_11_qn));  // open: Q, preset, reset
  D_Flip_Flop #(.trigger("high")) d_ff_12 (
    .D(undriven_2[2]), .clk(undriven_3), .Qn(d_ff_12_qn));  // open: Q, preset, reset
  D_Flip_Flop #(.trigger("high")) d_ff_13 (
    .D(undriven_2[3]), .clk(undriven_3), .Qn(d_ff_13_qn));  // open: Q, preset, reset
  D_Flip_Flop #(.trigger("high")) d_ff_14 (
    .D(undriven_2[4]), .clk(undriven_3), .Qn(d_ff_14_qn));  // open: Q, preset, reset
  D_Flip_Flop #(.trigger("high")) d_ff_15 (
    .D(undriven_2[5]), .clk(undriven_3), .Qn(d_ff_15_qn));  // open: Q, preset, reset
  D_Flip_Flop #(.trigger("high")) d_ff_16 (
    .D(undriven_2[6]), .clk(undriven_3), .Qn(d_ff_16_qn));  // open: Q, preset, reset
  D_Flip_Flop #(.trigger("high")) d_ff_17 (
    .D(undriven_2[7]), .clk(undriven_3), .Qn(d_ff_17_qn));  // open: Q, preset, reset
  D_Flip_Flop d_ff_18 (
    .D(d_ff_18_qn), .clk(not_8_out), .Q(d_ff_18_q), .Qn(d_ff_18_qn), .reset(not_1_out));  // open: preset
  D_Flip_Flop d_ff_19 (
    .D(d_ff_19_qn), .clk(not_9_out), .Q(d_ff_19_q), .Qn(d_ff_19_qn), .reset(not_1_out));  // open: preset
  clk_div clk_div_1 (.VCLK(VCLK), .Reset(d_ff_1_qn), .PAL(not_2_out), .out_4(clk_div_1_out_4));
  and and_2 (and_2_out, multiplexer_14_out, not_6_out, not_7_out);
  and and_3 (and_3_out, d_ff_8_q, buffer_2_out, not_7_out);
  and and_4 (and_4_out, d_ff_18_q, not_6_out, buffer_3_out);
  and and_5 (and_5_out, d_ff_31_q, buffer_2_out, buffer_3_out);
  and and_6 (and_6_out, d_ff_31_q, not_6_out, not_7_out);
  and and_7 (and_7_out, d_ff_9_q, buffer_2_out, not_7_out);
  and and_8 (and_8_out, d_ff_19_q, not_6_out, buffer_3_out);
  and and_9 (and_9_out, d_ff_32_q, buffer_2_out, buffer_3_out);
  not not_10 (not_10_out, d_ff_18_q);
  not not_11 (not_11_out, d_ff_19_q);
  Multiplexer multiplexer_5 (.in0(not_2_out), .in1(clk_div_1_out_4), .sel(TEST));  // open: out
  Multiplexer multiplexer_6 (.in0(d_ff_10_qn), .in1(d_ff_23_q), .out(multiplexer_6_out), .sel(nand_1_out));
  Multiplexer multiplexer_7 (.in0(d_ff_11_qn), .in1(d_ff_24_q), .out(multiplexer_7_out), .sel(nand_1_out));
  Multiplexer multiplexer_8 (.in0(d_ff_12_qn), .in1(d_ff_25_q), .out(multiplexer_8_out), .sel(nand_1_out));
  Multiplexer multiplexer_9 (.in0(d_ff_13_qn), .in1(d_ff_26_q), .out(multiplexer_9_out), .sel(nand_1_out));
  Multiplexer multiplexer_10 (.in0(d_ff_14_qn), .in1(d_ff_27_q), .out(multiplexer_10_out), .sel(nand_1_out));
  Multiplexer multiplexer_11 (.in0(d_ff_15_qn), .in1(d_ff_28_q), .out(multiplexer_11_out), .sel(nand_1_out));
  Multiplexer multiplexer_12 (.in0(d_ff_16_qn), .in1(d_ff_29_q), .out(multiplexer_12_out), .sel(nand_1_out));
  Multiplexer multiplexer_13 (.in0(d_ff_17_qn), .in1(1'b0), .out(multiplexer_13_out), .sel(nand_1_out));
  D_Flip_Flop d_ff_20 (
    .D(d_ff_20_qn), .clk(not_10_out), .Q(d_ff_20_q), .Qn(d_ff_20_qn), .reset(not_1_out));  // open: preset
  D_Flip_Flop d_ff_21 (
    .D(d_ff_21_qn), .clk(not_11_out), .Q(d_ff_21_q), .Qn(d_ff_21_qn), .reset(not_1_out));  // open: preset
  Multiplexer multiplexer_14 (.in0(clk_div_1_out_4), .in1(VCLK), .out(multiplexer_14_out), .sel(TEST));
  D_Flip_Flop d_ff_22 (.D(multiplexer_6_out), .clk(or_1_out), .Q(d_ff_22_q), .reset(not_14_out));  // open: Qn, preset
  D_Flip_Flop d_ff_23 (.D(multiplexer_7_out), .clk(or_1_out), .Q(d_ff_23_q), .reset(not_14_out));  // open: Qn, preset
  D_Flip_Flop d_ff_24 (.D(multiplexer_8_out), .clk(or_1_out), .Q(d_ff_24_q), .reset(not_14_out));  // open: Qn, preset
  D_Flip_Flop d_ff_25 (.D(multiplexer_9_out), .clk(or_1_out), .Q(d_ff_25_q), .reset(not_14_out));  // open: Qn, preset
  D_Flip_Flop d_ff_26 (.D(multiplexer_10_out), .clk(or_1_out), .Q(d_ff_26_q), .reset(not_14_out));  // open: Qn, preset
  D_Flip_Flop d_ff_27 (.D(multiplexer_11_out), .clk(or_1_out), .Q(d_ff_27_q), .reset(not_14_out));  // open: Qn, preset
  D_Flip_Flop d_ff_28 (.D(multiplexer_12_out), .clk(or_1_out), .Q(d_ff_28_q), .reset(not_14_out));  // open: Qn, preset
  D_Flip_Flop d_ff_29 (.D(multiplexer_13_out), .clk(or_1_out), .Q(d_ff_29_q), .reset(not_14_out));  // open: Qn, preset
  buf or_1 (or_1_out, or_3_out);  // OR_Gate
  or or_2 (or_2_out, and_2_out, and_3_out, and_4_out, and_5_out);
  or or_3 (or_3_out, and_6_out, and_7_out, and_8_out, and_9_out);
  not not_12 (not_12_out, d_ff_20_q);
  not not_13 (not_13_out, d_ff_21_q);
  not not_14 (not_14_out, d_ff_4_q);
  not not_15 (not_15_out, d_ff_22_q);
  D_Flip_Flop d_ff_30 (
    .D(nand_16_out), .clk(or_3_out), .Q(d_ff_30_q), .Qn(d_ff_30_qn), .reset(not_16_out));  // open: preset
  not not_16 (not_16_out, d_ff_1_q);
  or or_4 (or_4_out, d_ff_37_q, nor_3_out);
  or or_5 (or_5_out, nor_3_out, d_ff_33_qn);
  D_Flip_Flop d_ff_31 (
    .D(d_ff_31_qn), .clk(not_12_out), .Q(d_ff_31_q), .Qn(d_ff_31_qn), .reset(not_1_out));  // open: preset
  D_Flip_Flop d_ff_32 (
    .D(d_ff_32_qn), .clk(not_13_out), .Q(d_ff_32_q), .Qn(d_ff_32_qn), .reset(not_1_out));  // open: preset
  nand nand_1 (nand_1_out, d_ff_44_q, 1'b1, d_ff_39_qn, d_ff_34_qn, d_ff_36_qn, d_ff_30_qn);
  nand nand_2 (nand_2_out, d_ff_39_q, d_ff_30_qn);
  nand nand_3 (nand_3_out, d_ff_39_qn, d_ff_44_q, d_ff_30_qn);
  nand nand_4 (nand_4_out, d_ff_39_q, d_ff_34_q, d_ff_30_q);
  nand nand_5 (nand_5_out, d_ff_30_q, d_ff_34_q);
  nand nand_6 (nand_6_out, d_ff_34_q, d_ff_39_q, d_ff_36_q);
  nand nand_7 (nand_7_out, d_ff_39_q, d_ff_36_q, d_ff_30_q);
  nand nand_8 (nand_8_out, d_ff_39_q, d_ff_30_q);
  nand nand_9 (nand_9_out, d_ff_39_q, d_ff_34_q);
  D_Flip_Flop d_ff_33 (.D(nand_10_out), .clk(or_2_out), .Qn(d_ff_33_qn), .reset(not_19_out));  // open: Q, preset
  nand nand_10 (nand_10_out, or_4_out, or_5_out);
  not not_17 (not_17_out, nand_1_out);
  and and_10 (and_10_out, not_15_out, nand_1_out);
  D_Flip_Flop d_ff_34 (
    .D(nand_17_out), .clk(or_3_out), .Q(d_ff_34_q), .Qn(d_ff_34_qn), .reset(not_16_out));  // open: preset
  nand nand_11 (nand_11_out, d_ff_34_qn, d_ff_30_qn, d_ff_36_q, d_ff_39_q);
  not not_18 (not_18_out, d_ff_37_q);
  and and_11 (and_11_out, not_17_out, d_ff_38_q);
  nor nor_1 (nor_1_out, d_ff_38_q, undriven_6);
  D_Flip_Flop d_ff_35 (.D(and_10_out), .clk(or_3_out), .Q(d_ff_35_q), .preset(not_14_out));  // open: Qn, reset
  not not_19 (not_19_out, d_ff_1_q);
  not not_20 (not_20_out, and_16_out);
  nor nor_2 (nor_2_out, and_11_out, nor_1_out);
  not not_21 (not_21_out, d_ff_4_q);
  D_Flip_Flop d_ff_36 (
    .D(nand_18_out), .clk(or_3_out), .Q(d_ff_36_q), .Qn(d_ff_36_qn), .reset(not_16_out));  // open: preset
  D_Flip_Flop d_ff_37 (
    .D(nand_29_out), .clk(or_2_out), .Q(d_ff_37_q), .Qn(d_ff_37_qn), .preset(not_19_out));  // open: reset
  nor nor_3 (nor_3_out, d_ff_33_qn, not_20_out, d_ff_47_q);
  nand nand_12 (nand_12_out, d_ff_40_q, d_ff_43_q);
  not not_22 (not_22_out, or_3_out);
  and and_12 (and_12_out, d_ff_35_q, d_ff_4_q);
  buf and_13 (and_13_out, not_21_out);  // AND_Gate
  not not_23 (not_23_out, nor_3_out);
  nand nand_13 (nand_13_out, d_ff_40_q, d_ff_45_qn);
  nand nand_14 (nand_14_out, d_ff_45_qn, d_ff_43_q);
  nand nand_15 (nand_15_out, d_ff_43_qn, d_ff_45_q, d_ff_40_qn);
  not not_24 (not_24_out, undriven_4);
  D_Flip_Flop d_ff_38 (
    .D(nor_2_out), .clk(not_25_out), .Q(d_ff_38_q), .Qn(d_ff_38_qn), .preset(not_24_out), .reset(not_26_out));
  not not_25 (not_25_out, not_22_out);
  not not_26 (not_26_out, undriven_5);
  or or_6 (or_6_out, and_12_out, and_13_out);
  D_Flip_Flop d_ff_39 (
    .D(nand_19_out), .clk(or_3_out), .Q(d_ff_39_q), .Qn(d_ff_39_qn), .reset(not_16_out));  // open: preset
  nand nand_16 (nand_16_out, nand_2_out, nand_3_out, nand_4_out);
  nand nand_17 (nand_17_out, nand_3_out, nand_5_out, nand_11_out);
  nand nand_18 (nand_18_out, nand_3_out, nand_4_out, nand_6_out, nand_7_out);
  nand nand_19 (nand_19_out, nand_5_out, nand_11_out, nand_8_out, nand_9_out);
  nand nand_20 (nand_20_out, d_ff_39_q, d_ff_36_qn, d_ff_34_qn, d_ff_30_qn);
  D_Flip_Flop d_ff_40 (
    .D(nand_21_out), .clk(or_2_out), .Q(d_ff_40_q), .Qn(d_ff_40_qn), .preset(not_19_out));  // open: reset
  nand nand_21 (nand_21_out, not_23_out, nand_12_out, nand_15_out, nand_13_out);
  nand nand_22 (nand_22_out, nand_14_out, not_23_out, nand_24_out);
  nand nand_23 (nand_23_out, d_ff_45_q, nor_3_out);
  nand nand_24 (nand_24_out, d_ff_45_q, d_ff_43_qn);
  nand nand_25 (nand_25_out, d_ff_43_qn, d_ff_45_q, d_ff_40_qn, not_18_out);
  nand nand_26 (nand_26_out, d_ff_37_q, d_ff_40_q);
  nand nand_27 (nand_27_out, d_ff_37_q, d_ff_45_qn);
  nand nand_28 (nand_28_out, d_ff_37_q, d_ff_43_q);
  not not_27 (not_27_out, d_ff_38_qn);
  D_Flip_Flop d_ff_41 (
    .D(undriven_6), .clk(d_ff_42_q), .Q(d_ff_41_q), .preset(not_27_out), .reset(not_28_out));  // open: Qn
  not not_28 (not_28_out, undriven_7);
  buf buffer_4 (C4o, or_6_out);
  D_Flip_Flop d_ff_42 (.D(nand_20_out), .clk(or_3_out), .Q(d_ff_42_q), .preset(not_16_out));  // open: Qn, reset
  D_Flip_Flop d_ff_43 (
    .D(nand_23_out), .clk(or_2_out), .Q(d_ff_43_q), .Qn(d_ff_43_qn), .preset(not_19_out));  // open: reset
  nand nand_29 (nand_29_out, nand_25_out, 1'b1, not_23_out, nand_26_out, nand_27_out, nand_28_out);
  // AND_Gate and_14 has open pins: out=and_14_out
  D_Flip_Flop d_ff_44 (.D(d_ff_41_q), .clk(or_2_out), .Q(d_ff_44_q));  // open: Qn, preset, reset
  D_Flip_Flop d_ff_45 (
    .D(nand_22_out), .clk(or_2_out), .Q(d_ff_45_q), .Qn(d_ff_45_qn), .reset(not_19_out));  // open: preset
  not not_29 (not_29_out, d_ff_5_q);
  not not_30 (not_30_out, and_14_out);
  not not_31 (not_31_out, 1'b1);
  and and_15 (and_15_out, d_ff_47_q, 1'b1);
  D_Flip_Flop d_ff_46 (.D(and_15_out), .clk(d_ff_37_qn), .Q(d_ff_46_q), .reset(not_32_out));  // open: Qn, preset
  D_Flip_Flop d_ff_47 (.D(C5i), .clk(or_2_out), .Q(d_ff_47_q), .Qn(d_ff_47_qn), .preset(not_29_out));  // open: reset
  D_Flip_Flop d_ff_48 (.D(1'b1), .clk(or_7_out), .reset(not_30_out));  // open: Q, Qn, preset
  D_Flip_Flop d_ff_49 (
    .D(xor_delay_6x_1_out_2), .clk(or_7_out), .Q(d_ff_68_q[7]), .reset(not_31_out));  // open: Qn, preset
  D_Flip_Flop d_ff_50 (.D(d_ff_46_q), .clk(d_ff_37_qn), .Q(d_ff_50_q), .reset(not_32_out));  // open: Qn, preset
  not not_32 (not_32_out, d_ff_5_q);
  nand nand_30 (nand_30_out, d_ff_56_q, d_ff_67_q);
  D_Flip_Flop d_ff_51 (.D(d_ff_47_qn), .clk(or_7_out), .reset(not_30_out));  // open: Q, Qn, preset
  xor_delay_6x xor_delay_6x_1 (.in_1(d_ff_46_q), .out_2(xor_delay_6x_1_out_2));
  nand nand_31 (nand_31_out, d_ff_56_qn, d_ff_67_qn, d_ff_33_qn, not_33_out);
  nand nand_32 (nand_32_out, d_ff_56_q, d_ff_59_q, d_ff_64_qn, d_ff_67_qn);
  not not_33 (not_33_out, d_ff_47_q);
  D_Flip_Flop d_ff_52 (
    .D(xor_delay_6x_2_out_2), .clk(or_7_out), .Q(d_ff_68_q[6]), .reset(not_31_out));  // open: Qn, preset
  xor_delay_6x xor_delay_6x_2 (.in_1(d_ff_50_q), .out_2(xor_delay_6x_2_out_2));
  D_Flip_Flop d_ff_53 (.D(d_ff_50_q), .clk(d_ff_37_qn), .Q(d_ff_53_q), .reset(not_32_out));  // open: Qn, preset
  not not_34 (not_34_out, d_ff_1_q);
  nand nand_33 (nand_33_out, nand_31_out, nand_32_out, nand_34_out, nand_30_out);
  and and_16 (and_16_out, d_ff_56_qn, d_ff_67_qn);
  nand nand_34 (nand_34_out, d_ff_64_q, d_ff_67_qn, d_ff_56_q);
  nand nand_35 (nand_35_out, d_ff_56_q, d_ff_67_qn, d_ff_59_qn);
  nand nand_36 (nand_36_out, d_ff_56_q, d_ff_64_q, d_ff_67_q);
  nand nand_37 (nand_37_out, d_ff_64_q, d_ff_56_q, d_ff_59_q);
  nand nand_38 (nand_38_out, d_ff_67_q, d_ff_56_q, d_ff_59_q);
  D_Flip_Flop d_ff_54 (
    .D(xor_delay_6x_3_out_2), .clk(or_7_out), .Q(d_ff_68_q[5]), .reset(not_31_out));  // open: Qn, preset
  xor_delay_6x xor_delay_6x_3 (.in_1(d_ff_53_q), .out_2(xor_delay_6x_3_out_2));
  D_Flip_Flop d_ff_55 (.D(d_ff_53_q), .clk(d_ff_37_qn), .Q(d_ff_55_q), .reset(not_32_out));  // open: Qn, preset
  D_Flip_Flop d_ff_56 (
    .D(nand_33_out), .clk(d_ff_37_qn), .Q(d_ff_56_q), .Qn(d_ff_56_qn), .reset(not_34_out));  // open: preset
  nand nand_39 (nand_39_out, nand_32_out, nand_31_out, nand_34_out, nand_35_out);
  nand nand_40 (nand_40_out, nand_35_out, nand_31_out, nand_32_out, nand_36_out);
  nand nand_41 (nand_41_out, nand_35_out, nand_31_out, nand_37_out, nand_38_out);
  D_Flip_Flop d_ff_57 (
    .D(xor_delay_6x_4_out_2), .clk(or_7_out), .Q(d_ff_68_q[4]), .reset(not_31_out));  // open: Qn, preset
  xor_delay_6x xor_delay_6x_4 (.in_1(d_ff_55_q), .out_2(xor_delay_6x_4_out_2));
  D_Flip_Flop d_ff_58 (.D(d_ff_55_q), .clk(d_ff_37_qn), .Q(d_ff_58_q), .reset(not_35_out));  // open: Qn, preset
  D_Flip_Flop d_ff_59 (
    .D(nand_41_out), .clk(d_ff_37_qn), .Q(d_ff_59_q), .Qn(d_ff_59_qn), .reset(not_34_out));  // open: preset
  D_Flip_Flop d_ff_60 (
    .D(xor_delay_6x_5_out_2), .clk(or_7_out), .Q(d_ff_68_q[3]), .reset(not_31_out));  // open: Qn, preset
  D_Flip_Flop d_ff_61 (.D(d_ff_58_q), .clk(d_ff_37_qn), .Q(d_ff_61_q), .reset(not_35_out));  // open: Qn, preset
  not not_35 (not_35_out, d_ff_5_q);
  D_Flip_Flop d_ff_62 (
    .D(xor_delay_6x_6_out_2), .clk(or_7_out), .Q(d_ff_68_q[2]), .reset(not_31_out));  // open: Qn, preset
  xor_delay_6x xor_delay_6x_5 (.in_1(d_ff_58_q), .out_2(xor_delay_6x_5_out_2));
  D_Flip_Flop d_ff_63 (.D(d_ff_61_q), .clk(d_ff_37_qn), .Q(d_ff_63_q), .reset(not_35_out));  // open: Qn, preset
  D_Flip_Flop d_ff_64 (
    .D(nand_40_out), .clk(d_ff_37_qn), .Q(d_ff_64_q), .Qn(d_ff_64_qn), .reset(not_34_out));  // open: preset
  xor_delay_6x xor_delay_6x_6 (.in_1(d_ff_61_q), .out_2(xor_delay_6x_6_out_2));
  D_Flip_Flop d_ff_65 (
    .D(xor_delay_6x_7_out_2), .clk(or_7_out), .Q(d_ff_68_q[1]), .reset(not_31_out));  // open: Qn, preset
  xor_delay_6x xor_delay_6x_7 (.in_1(d_ff_63_q), .out_2(xor_delay_6x_7_out_2));
  D_Flip_Flop d_ff_66 (.D(d_ff_63_q), .clk(d_ff_37_qn), .Q(d_ff_66_q), .reset(not_35_out));  // open: Qn, preset
  D_Flip_Flop d_ff_67 (
    .D(nand_39_out), .clk(d_ff_37_qn), .Q(d_ff_67_q), .Qn(d_ff_67_qn), .reset(not_34_out));  // open: preset
  D_Flip_Flop d_ff_68 (
    .D(xor_delay_6x_8_out_2), .clk(or_7_out), .Q(d_ff_68_q[0]), .reset(not_31_out));  // open: Qn, preset
  xor_delay_6x xor_delay_6x_8 (.in_1(d_ff_66_q), .out_2(xor_delay_6x_8_out_2));
  D_Flip_Flop d_ff_69 (.D(nand_35_out), .clk(d_ff_37_qn), .Q(d_ff_69_q), .preset(not_34_out));  // open: Qn, reset
  or or_7 (or_7_out, d_ff_69_q, d_ff_37_qn);

  // Notes on the sheet:
  //   w5
endmodule

module cnt_bit (
  input  cin,
  input  val,
  input  load,
  input  clk,
  input  res,
  output cout,
  output q,
  output nq
);

  wire multiplexer_1_out, not_1_out, xor_1_out;

  and and_1 (cout, cin, q);
  xor xor_1 (xor_1_out, cin, q);
  not not_1 (not_1_out, res);
  Multiplexer multiplexer_1 (.in0(val), .in1(xor_1_out), .out(multiplexer_1_out), .sel(load));
  D_Flip_Flop d_ff_1 (.D(multiplexer_1_out), .clk(clk), .Q(q), .Qn(nq), .reset(not_1_out));  // open: preset
endmodule

module clk_div (
  input  VCLK,
  input  Reset,
  input  PAL,
  output out_4
);

  wire and_1_out, and_2_out, and_3_out, and_4_out, cnt_bit_1_cout, cnt_bit_1_nq, cnt_bit_2_cout,
       cnt_bit_2_nq, cnt_bit_3_cout, cnt_bit_3_nq, cnt_bit_4_cout, cnt_bit_4_nq, cnt_bit_5_cout,
       cnt_bit_5_nq, cnt_bit_6_cout, cnt_bit_6_nq, cnt_bit_7_nq, cnt_bit_8_nq, nor_1_out, nor_2_out,
       nor_3_out;

  and and_1 (and_1_out, nor_3_out, 1'b1, and_4_out);
  and and_2 (and_2_out, nor_3_out, 1'b1, 1'b1);
  cnt_bit cnt_bit_1 (
    .cin(and_1_out), .val(1'b1), .load(nor_3_out), .clk(VCLK), .res(1'b1), .cout(cnt_bit_1_cout),
    .nq(cnt_bit_1_nq));  // open: q
  cnt_bit cnt_bit_2 (
    .cin(and_2_out), .val(PAL), .load(nor_3_out), .clk(VCLK), .res(1'b1), .cout(cnt_bit_2_cout),
    .nq(cnt_bit_2_nq));  // open: q
  nor nor_1 (nor_1_out, cnt_bit_1_nq, cnt_bit_3_nq, cnt_bit_5_nq, cnt_bit_7_nq);
  nor nor_2 (nor_2_out, cnt_bit_2_nq, cnt_bit_8_nq, cnt_bit_6_nq, cnt_bit_4_nq);
  cnt_bit cnt_bit_3 (
    .cin(cnt_bit_1_cout), .val(1'b0), .load(nor_3_out), .clk(VCLK), .res(1'b1), .cout(cnt_bit_3_cout),
    .nq(cnt_bit_3_nq));  // open: q
  and and_3 (and_3_out, nor_1_out, and_4_out);
  cnt_bit cnt_bit_4 (
    .cin(cnt_bit_2_cout), .val(1'b0), .load(nor_3_out), .clk(VCLK), .res(1'b1), .cout(cnt_bit_4_cout),
    .nq(cnt_bit_4_nq));  // open: q
  and and_4 (and_4_out, nor_2_out, 1'b1);
  nor nor_3 (nor_3_out, Reset, and_3_out);
  cnt_bit cnt_bit_5 (
    .cin(cnt_bit_3_cout), .val(1'b0), .load(nor_3_out), .clk(VCLK), .res(1'b1), .cout(cnt_bit_5_cout),
    .q(out_4), .nq(cnt_bit_5_nq));
  cnt_bit cnt_bit_6 (
    .cin(cnt_bit_4_cout), .val(1'b1), .load(nor_3_out), .clk(VCLK), .res(1'b1), .cout(cnt_bit_6_cout),
    .nq(cnt_bit_6_nq));  // open: q
  cnt_bit cnt_bit_7 (
    .cin(cnt_bit_5_cout), .val(1'b1), .load(nor_3_out), .clk(VCLK), .res(1'b1), .nq(cnt_bit_7_nq));  // open: cout, q
  cnt_bit cnt_bit_8 (
    .cin(cnt_bit_6_cout), .val(1'b1), .load(nor_3_out), .clk(VCLK), .res(1'b1), .nq(cnt_bit_8_nq));  // open: cout, q
endmodule

module xor_delay_6x (
  input  in_1,
  output out_2
);

  wire xor_1_out, xor_2_out, xor_3_out, xor_4_out, xor_5_out;

  xor xor_1 (xor_1_out, in_1, 1'b0);
  xor xor_2 (xor_2_out, xor_1_out, 1'b0);
  xor xor_3 (xor_3_out, xor_2_out, 1'b0);
  xor xor_4 (xor_4_out, xor_3_out, 1'b0);
  xor xor_5 (xor_5_out, xor_4_out, 1'b0);
  xor xor_6 (out_2, xor_5_out, 1'b0);
endmodule
