// Logisim project YM3438.circ as structural Verilog
module CLOCK (
  input  M,
  input  g_932
);

  wire _1_out, _3_out, _6_out, _15_out, _16_out, _20_out, _24_out, _25_out, _95_out, _96_out, C1, C2,
       clock_1_out, cnt_bit_1_co, cnt_bit_1_q, cnt_bit_2_q, cnt_bit_3_co, cnt_bit_3_q, cnt_bit_4_co,
       cnt_bit_4_q, cnt_bit_5_q, FCLK1, FCLK2, nFCLK1, nFCLK2, not_1_out, not_2_out, not_3_out, not_4_out,
       not_5_out, not_6_out, not_8_out, not_9_out, not_10_out, not_11_out, not_12_out, not_13_out,
       not_15_out, not_16_out, not_17_out, not_18_out, not_19_out, not_20_out, not_21_out, not_22_out,
       not_23_out, not_24_out, not_25_out, not_26_out, not_27_out, not_28_out, not_29_out, not_31_out,
       not_33_out, not_35_out, not_36_out, sdelay12_1_q, sr_bit_1_q, sr_bit_2_q, sr_bit_3_q, sr_bit_4_q,
       sr_bit_5_q, sr_bit_6_q, sr_bit_7_q, sr_bit_8_q, sr_bit_9_q, sr_bit_10_q, sr_bit_11_q, sr_bit_12_q;

  Clock clock_1 (.out(clock_1_out));
  not not_1 (not_1_out, clock_1_out);
  not not_2 (not_2_out, g_932);
  nor _1 (_1_out, not_1_out, not_13_out);
  nor _3 (_3_out, not_9_out, clock_1_out);
  SR_BIT sr_bit_1 (.C2(C2), .C1(C1), .D(_15_out), .Q(sr_bit_1_q));  // open: nQ
  SDELAY12 sdelay12_1 (.C2(C2), .C1(C1), .D(not_2_out), .Q(sdelay12_1_q));
  SR_BIT sr_bit_2 (.C2(C2), .C1(C1), .D(_16_out), .Q(sr_bit_2_q));  // open: nQ
  not not_3 (not_3_out, _1_out);
  not not_4 (not_4_out, _1_out);
  not not_5 (not_5_out, _3_out);
  not not_6 (not_6_out, _3_out);
  not not_7 (C2, not_3_out);
  not not_8 (not_8_out, not_10_out);
  not not_9 (not_9_out, not_8_out);
  not not_10 (not_10_out, not_4_out);
  not not_11 (not_11_out, not_12_out);
  not not_12 (not_12_out, not_5_out);
  not not_13 (not_13_out, not_11_out);
  not not_14 (C1, not_6_out);
  SR_BIT sr_bit_3 (.C2(C2), .C1(C1), .D(sr_bit_1_q), .Q(sr_bit_3_q));  // open: nQ
  SR_BIT sr_bit_4 (.C2(C2), .C1(C1), .D(sr_bit_2_q), .Q(sr_bit_4_q));  // open: nQ
  not not_15 (not_15_out, sdelay12_1_q);
  SR_BIT sr_bit_5 (.C2(C2), .C1(C1), .D(sr_bit_3_q), .Q(sr_bit_5_q));  // open: nQ
  and _15 (_15_out, not_15_out, not_2_out);
  SR_BIT sr_bit_6 (.C2(C2), .C1(C1), .D(sr_bit_4_q), .Q(sr_bit_6_q));  // open: nQ
  SR_BIT sr_bit_7 (.C2(C2), .C1(C1), .D(sr_bit_5_q), .Q(sr_bit_7_q));  // open: nQ
  SR_BIT sr_bit_8 (.C2(C2), .C1(C1), .D(sr_bit_6_q), .Q(sr_bit_8_q));  // open: nQ
  or _6 (_6_out, sr_bit_7_q, cnt_bit_2_q);
  CNT_BIT cnt_bit_1 (.C2(FCLK2), .C1(FCLK1), .CIN(1'b1), .RES(_6_out), .Q(cnt_bit_1_q), .CO(cnt_bit_1_co));  // open: nQ
  CNT_BIT cnt_bit_2 (.C2(FCLK2), .C1(FCLK1), .CIN(cnt_bit_1_co), .RES(_6_out), .Q(cnt_bit_2_q));  // open: nQ, CO
  CNT_BIT cnt_bit_3 (
    .C2(FCLK2), .C1(FCLK1), .CIN(cnt_bit_2_q), .RES(sr_bit_7_q), .Q(cnt_bit_3_q), .CO(cnt_bit_3_co));  // open: nQ
  CNT_BIT cnt_bit_4 (
    .C2(FCLK2), .C1(FCLK1), .CIN(cnt_bit_3_co), .RES(sr_bit_7_q), .Q(cnt_bit_4_q), .CO(cnt_bit_4_co));  // open: nQ
  CNT_BIT cnt_bit_5 (.C2(FCLK2), .C1(FCLK1), .CIN(cnt_bit_4_co), .RES(sr_bit_7_q), .Q(cnt_bit_5_q));  // open: nQ, CO
  SR_BIT sr_bit_9 (.C2(C2), .C1(C1), .D(sr_bit_8_q), .Q(sr_bit_9_q));  // open: nQ
  or _25 (_25_out, sr_bit_10_q, sr_bit_2_q);
  or _24 (_24_out, sr_bit_8_q, sr_bit_6_q);
  not not_16 (not_16_out, cnt_bit_1_q);
  not not_17 (not_17_out, cnt_bit_2_q);
  not not_18 (not_18_out, cnt_bit_3_q);
  not not_19 (not_19_out, cnt_bit_4_q);
  not not_20 (not_20_out, cnt_bit_5_q);
  not not_21 (not_21_out, not_16_out);
  not not_22 (not_22_out, not_17_out);
  not not_23 (not_23_out, not_18_out);
  not not_24 (not_24_out, not_19_out);
  not not_25 (not_25_out, not_20_out);
  or _20 (_20_out, sr_bit_2_q, sr_bit_4_q, sr_bit_6_q, sr_bit_8_q, sr_bit_9_q);
  SR_BIT sr_bit_10 (.C2(C2), .C1(C1), .D(sr_bit_9_q), .Q(sr_bit_10_q));  // open: nQ
  SR_BIT sr_bit_11 (.C2(C2), .C1(C1), .D(_25_out), .Q(sr_bit_11_q));  // open: nQ
  SR_BIT sr_bit_12 (.C2(C2), .C1(C1), .D(_24_out), .Q(sr_bit_12_q));  // open: nQ
  nor _16 (_16_out, _15_out, _20_out);
  not not_26 (not_26_out, sr_bit_11_q);
  not not_27 (not_27_out, sr_bit_12_q);
  not not_28 (not_28_out, not_26_out);
  not not_29 (not_29_out, not_27_out);
  not not_30 (FCLK1, not_31_out);
  not not_31 (not_31_out, not_28_out);
  not not_32 (nFCLK1, not_33_out);
  not not_33 (not_33_out, not_26_out);
  not not_34 (FCLK2, not_35_out);
  not not_35 (not_35_out, not_29_out);
  not not_36 (not_36_out, not_27_out);
  not not_37 (nFCLK2, not_36_out);
  buf _95 (_95_out, not_21_out);  // AND_Gate
  buf _96 (_96_out, not_21_out);  // AND_Gate
  // AND_Gate _94 is placed but not wired
  // AND_Gate _93 is placed but not wired
  // AND_Gate _92 is placed but not wired
  // AND_Gate _91 is placed but not wired
  // AND_Gate _94_2 is placed but not wired
  // AND_Gate _93_2 is placed but not wired
  // AND_Gate _92_2 is placed but not wired
  // AND_Gate _91_2 is placed but not wired

  // Notes on the sheet:
  //   38
  //   9
  //   12
  //   17
  //   7A
  //   7B
  //   10
  //   7A
  //   2
  //   39
  //   7B
  //   /C2
  //   C2
  //   /C1
  //   C1
  //   13
  //   14
  //   18
  //   8
  //   19
  //   11
  //   21
  //   43
  //   42
  //   40
  //   4
  //   5
  //   22
  //   97
  //   98
  //   99
  //   41
  //   44
  //   97
  //   98
  //   99
  //   41
  //   44
  //   23
  //   27
  //   26
  //   35
  //   30
  //   35
  //   30
  //   34
  //   33
  //   37
  //   36
  //   29
  //   28
  //   31
  //   32
endmodule

module D_LATCH (
  input  EN,
  input  D,
  output Q,
  output nQ
);

  D_Flip_Flop #(.trigger("high")) d_ff_1 (.clk(EN), .D(D), .Q(Q), .Qn(nQ));  // open: preset, en, reset
endmodule

// SR BIT
module SR_BIT (
  input  C2,
  input  C1,
  input  D,
  output Q,
  output nQ
);

  wire d_latch_1_q;

  D_LATCH d_latch_1 (.EN(C1), .D(D), .Q(d_latch_1_q));  // open: nQ
  D_LATCH d_latch_2 (.EN(C2), .D(d_latch_1_q), .Q(Q), .nQ(nQ));
endmodule

module SDELAY12 (
  input  C2,
  input  C1,
  input  D,
  output Q
);

  wire d_ff_1_q, d_ff_2_q, d_ff_3_q, d_ff_4_q, d_ff_5_q, d_ff_6_q, d_ff_7_q, d_ff_8_q, d_ff_9_q, d_ff_10_q,
       d_ff_11_q, d_ff_12_q, d_ff_13_q, d_ff_14_q, d_ff_15_q, d_ff_16_q, d_ff_17_q, d_ff_18_q, d_ff_19_q,
       d_ff_20_q, d_ff_21_q, d_ff_22_q, d_ff_23_q;

  D_Flip_Flop #(.trigger("high")) d_ff_1 (.clk(C1), .D(D), .Q(d_ff_1_q));  // open: Qn, preset, en, reset
  D_Flip_Flop #(.trigger("high")) d_ff_2 (.clk(C1), .D(d_ff_22_q), .Q(d_ff_2_q));  // open: Qn, preset, en, reset
  D_Flip_Flop #(.trigger("high")) d_ff_3 (.clk(C1), .D(d_ff_23_q), .Q(d_ff_3_q));  // open: Qn, preset, en, reset
  D_Flip_Flop #(.trigger("high")) d_ff_4 (.clk(C2), .D(d_ff_1_q), .Q(d_ff_4_q));  // open: Qn, preset, en, reset
  D_Flip_Flop #(.trigger("high")) d_ff_5 (.clk(C2), .D(d_ff_2_q), .Q(d_ff_5_q));  // open: Qn, preset, en, reset
  D_Flip_Flop #(.trigger("high")) d_ff_6 (.clk(C2), .D(d_ff_3_q), .Q(d_ff_6_q));  // open: Qn, preset, en, reset
  D_Flip_Flop #(.trigger("high")) d_ff_7 (.clk(C1), .D(d_ff_4_q), .Q(d_ff_7_q));  // open: Qn, preset, en, reset
  D_Flip_Flop #(.trigger("high")) d_ff_8 (.clk(C1), .D(d_ff_5_q), .Q(d_ff_8_q));  // open: Qn, preset, en, reset
  D_Flip_Flop #(.trigger("high")) d_ff_9 (.clk(C1), .D(d_ff_6_q), .Q(d_ff_9_q));  // open: Qn, preset, en, reset
  D_Flip_Flop #(.trigger("high")) d_ff_10 (.clk(C2), .D(d_ff_7_q), .Q(d_ff_10_q));  // open: Qn, preset, en, reset
  D_Flip_Flop #(.trigger("high")) d_ff_11 (.clk(C2), .D(d_ff_8_q), .Q(d_ff_11_q));  // open: Qn, preset, en, reset
  D_Flip_Flop #(.trigger("high")) d_ff_12 (.clk(C2), .D(d_ff_9_q), .Q(d_ff_12_q));  // open: Qn, preset, en, reset
  D_Flip_Flop #(.trigger("high")) d_ff_13 (.clk(C1), .D(d_ff_10_q), .Q(d_ff_13_q));  // open: Qn, preset, en, reset
  D_Flip_Flop #(.trigger("high")) d_ff_14 (.clk(C1), .D(d_ff_11_q), .Q(d_ff_14_q));  // open: Qn, preset, en, reset
  D_Flip_Flop #(.trigger("high")) d_ff_15 (.clk(C1), .D(d_ff_12_q), .Q(d_ff_15_q));  // open: Qn, preset, en, reset
  D_Flip_Flop #(.trigger("high")) d_ff_16 (.clk(C2), .D(d_ff_13_q), .Q(d_ff_16_q));  // open: Qn, preset, en, reset
  D_Flip_Flop #(.trigger("high")) d_ff_17 (.clk(C2), .D(d_ff_14_q), .Q(d_ff_17_q));  // open: Qn, preset, en, reset
  D_Flip_Flop #(.trigger("high")) d_ff_18 (.clk(C2), .D(d_ff_15_q), .Q(d_ff_18_q));  // open: Qn, preset, en, reset
  D_Flip_Flop #(.trigger("high")) d_ff_19 (.clk(C1), .D(d_ff_16_q), .Q(d_ff_19_q));  // open: Qn, preset, en, reset
  D_Flip_Flop #(.trigger("high")) d_ff_20 (.clk(C1), .D(d_ff_17_q), .Q(d_ff_20_q));  // open: Qn, preset, en, reset
  D_Flip_Flop #(.trigger("high")) d_ff_21 (.clk(C1), .D(d_ff_18_q), .Q(d_ff_21_q));  // open: Qn, preset, en, reset
  D_Flip_Flop #(.trigger("high")) d_ff_22 (.clk(C2), .D(d_ff_19_q), .Q(d_ff_22_q));  // open: Qn, preset, en, reset
  D_Flip_Flop #(.trigger("high")) d_ff_23 (.clk(C2), .D(d_ff_20_q), .Q(d_ff_23_q));  // open: Qn, preset, en, reset
  D_Flip_Flop #(.trigger("high")) d_ff_24 (.clk(C2), .D(d_ff_21_q), .Q(Q));  // open: Qn, preset, en, reset
endmodule

// CNT BIT
module CNT_BIT (
  input  C2,
  input  C1,
  input  CIN,
  input  RES,
  output Q,
  output nQ,
  output CO
);

  wire and_1_out, d_ff_1_q, not_1_out, xor_1_out;

  not not_1 (not_1_out, RES);
  and and_1 (and_1_out, not_1_out, xor_1_out);
  xor xor_1 (xor_1_out, Q, CIN);
  and and_2 (CO, Q, CIN);
  D_Flip_Flop #(.trigger("high")) d_ff_1 (.clk(C1), .D(and_1_out), .Q(d_ff_1_q));  // open: Qn, preset, en, reset
  D_Flip_Flop #(.trigger("high")) d_ff_2 (.clk(C2), .D(d_ff_1_q), .Q(Q), .Qn(nQ));  // open: preset, en, reset
endmodule
