// Logisim project ymcells.circ as structural Verilog: 48 circuits, main circuit cell32
module cell32 (
  input  in_1,
  output out_2
);

  wire transistor_1_out, transistor_2_out, transistor_5_out;

  Transistor transistor_1 (.in(1'b1), .out(transistor_1_out), .gate(transistor_2_out));
  Transistor transistor_2 (.in(1'b1), .out(transistor_2_out), .gate(in_1));
  Transistor #(.\type ("n")) transistor_3 (.in(1'b0), .out(transistor_2_out), .gate(in_1));
  Transistor #(.\type ("n")) transistor_4 (.in(1'b0), .out(transistor_1_out), .gate(transistor_2_out));
  Transistor transistor_5 (.in(1'b1), .out(transistor_5_out), .gate(transistor_1_out));
  Transistor #(.\type ("n")) transistor_6 (.in(1'b0), .out(transistor_5_out), .gate(transistor_1_out));
  Transistor transistor_7 (.in(1'b1), .out(out_2), .gate(transistor_5_out));
  Transistor #(.\type ("n")) transistor_8 (.in(1'b0), .out(out_2), .gate(transistor_5_out));
endmodule

module cell33 (
  input  a,
  output b,
  output c
);

  wire transistor_5_out;

  Transistor transistor_1 (.in(1'b1), .out(b), .gate(a));
  Transistor transistor_2 (.in(1'b1), .out(b), .gate(a));
  Transistor #(.\type ("n")) transistor_3 (.in(1'b0), .out(b), .gate(a));
  Transistor #(.\type ("n")) transistor_4 (.in(1'b0), .out(b), .gate(a));
  Transistor transistor_5 (.in(1'b1), .out(transistor_5_out), .gate(a));
  Transistor #(.\type ("n")) transistor_6 (.in(1'b0), .out(transistor_5_out), .gate(a));
  Transistor transistor_7 (.in(1'b1), .out(c), .gate(transistor_5_out));
  Transistor transistor_8 (.in(1'b1), .out(c), .gate(transistor_5_out));
  Transistor #(.\type ("n")) transistor_9 (.in(1'b0), .out(c), .gate(transistor_5_out));
  Transistor #(.\type ("n")) transistor_10 (.in(1'b0), .out(c), .gate(transistor_5_out));
endmodule

module cell35 (
  input  b,
  input  c,
  input  d,
  input  e,
  input  f,
  output a
);

  wire transistor_1_out, transistor_2_out, transistor_5_out, transistor_6_out, transistor_7_out,
       transistor_14_out;

  Transistor transistor_1 (.in(1'b1), .out(transistor_1_out), .gate(b));
  Transistor transistor_2 (.in(transistor_1_out), .out(transistor_2_out), .gate(c));
  Transistor #(.\type ("n")) transistor_3 (.in(1'b0), .out(transistor_2_out), .gate(c));
  Transistor #(.\type ("n")) transistor_4 (.in(1'b0), .out(transistor_2_out), .gate(b));
  Transistor transistor_5 (.in(1'b1), .out(transistor_5_out), .gate(d));
  Transistor transistor_6 (.in(transistor_5_out), .out(transistor_6_out), .gate(e));
  Transistor transistor_7 (.in(transistor_6_out), .out(transistor_7_out), .gate(f));
  Transistor #(.\type ("n")) transistor_8 (.in(1'b0), .out(transistor_7_out), .gate(e));
  Transistor #(.\type ("n")) transistor_9 (.in(1'b0), .out(transistor_7_out), .gate(d));
  Transistor transistor_10 (.in(1'b1), .out(a), .gate(transistor_2_out));
  Transistor #(.\type ("n")) transistor_11 (.in(1'b0), .out(transistor_7_out), .gate(f));
  Transistor transistor_12 (.in(1'b1), .out(a), .gate(transistor_7_out));
  Transistor #(.\type ("n")) transistor_13 (.in(transistor_14_out), .out(a), .gate(transistor_2_out));
  Transistor #(.\type ("n")) transistor_14 (.in(1'b0), .out(transistor_14_out), .gate(transistor_7_out));
endmodule

module cell36 (
  input  a,
  input  b,
  input  c,
  input  d,
  output e
);

  wire transistor_1_out, transistor_2_out, transistor_3_out;

  Transistor transistor_1 (.in(1'b1), .out(transistor_1_out), .gate(a));
  Transistor transistor_2 (.in(transistor_1_out), .out(transistor_2_out), .gate(b));
  Transistor transistor_3 (.in(transistor_2_out), .out(transistor_3_out), .gate(c));
  Transistor transistor_4 (.in(transistor_3_out), .out(e), .gate(d));
  Transistor #(.\type ("n")) transistor_5 (.in(1'b0), .out(e), .gate(a));
  Transistor #(.\type ("n")) transistor_6 (.in(1'b0), .out(e), .gate(b));
  Transistor #(.\type ("n")) transistor_7 (.in(1'b0), .out(e), .gate(c));
  Transistor #(.\type ("n")) transistor_8 (.in(1'b0), .out(e), .gate(d));
endmodule

module cell37 (
  input  a,
  input  b,
  input  c,
  input  d,
  output e
);

  wire transistor_4_out, transistor_5_out, transistor_6_out;

  Transistor transistor_1 (.in(1'b1), .out(e), .gate(c));
  Transistor transistor_2 (.in(1'b1), .out(e), .gate(d));
  Transistor #(.\type ("n")) transistor_3 (.in(transistor_4_out), .out(e), .gate(a));
  Transistor #(.\type ("n")) transistor_4 (.in(transistor_5_out), .out(transistor_4_out), .gate(b));
  Transistor #(.\type ("n")) transistor_5 (.in(transistor_6_out), .out(transistor_5_out), .gate(c));
  Transistor #(.\type ("n")) transistor_6 (.in(1'b0), .out(transistor_6_out), .gate(d));
  Transistor transistor_7 (.in(1'b1), .out(e), .gate(b));
  Transistor transistor_8 (.in(1'b1), .out(e), .gate(a));
endmodule

module cell38 (
  input  a,
  input  b,
  input  c,
  input  d,
  input  e,
  input  f,
  output g
);

  wire transistor_1_out, transistor_2_out, transistor_3_out, transistor_6_out, transistor_7_out,
       transistor_8_out, transistor_16_out;

  Transistor transistor_1 (.in(1'b1), .out(transistor_1_out), .gate(a));
  Transistor transistor_2 (.in(transistor_1_out), .out(transistor_2_out), .gate(b));
  Transistor transistor_3 (.in(transistor_2_out), .out(transistor_3_out), .gate(c));
  Transistor #(.\type ("n")) transistor_4 (.in(1'b0), .out(transistor_3_out), .gate(b));
  Transistor #(.\type ("n")) transistor_5 (.in(1'b0), .out(transistor_3_out), .gate(a));
  Transistor transistor_6 (.in(1'b1), .out(transistor_6_out), .gate(d));
  Transistor transistor_7 (.in(transistor_6_out), .out(transistor_7_out), .gate(e));
  Transistor transistor_8 (.in(transistor_7_out), .out(transistor_8_out), .gate(f));
  Transistor #(.\type ("n")) transistor_9 (.in(1'b0), .out(transistor_8_out), .gate(e));
  Transistor #(.\type ("n")) transistor_10 (.in(1'b0), .out(transistor_8_out), .gate(d));
  Transistor #(.\type ("n")) transistor_11 (.in(1'b0), .out(transistor_3_out), .gate(c));
  Transistor transistor_12 (.in(1'b1), .out(g), .gate(transistor_3_out));
  Transistor #(.\type ("n")) transistor_13 (.in(1'b0), .out(transistor_8_out), .gate(f));
  Transistor transistor_14 (.in(1'b1), .out(g), .gate(transistor_8_out));
  Transistor #(.\type ("n")) transistor_15 (.in(transistor_16_out), .out(g), .gate(transistor_3_out));
  Transistor #(.\type ("n")) transistor_16 (.in(1'b0), .out(transistor_16_out), .gate(transistor_8_out));
endmodule

module cell39 (
  input  a,
  input  b,
  input  c,
  input  d,
  input  e,
  input  f,
  output g
);

  wire transistor_1_out, transistor_2_out, transistor_3_out, transistor_6_out, transistor_7_out,
       transistor_8_out, transistor_12_out, transistor_16_out;

  Transistor transistor_1 (.in(1'b1), .out(transistor_1_out), .gate(a));
  Transistor transistor_2 (.in(transistor_1_out), .out(transistor_2_out), .gate(b));
  Transistor transistor_3 (.in(transistor_2_out), .out(transistor_3_out), .gate(c));
  Transistor #(.\type ("n")) transistor_4 (.in(1'b0), .out(transistor_3_out), .gate(a));
  Transistor #(.\type ("n")) transistor_5 (.in(1'b0), .out(transistor_3_out), .gate(b));
  Transistor transistor_6 (.in(1'b1), .out(transistor_6_out), .gate(d));
  Transistor transistor_7 (.in(transistor_6_out), .out(transistor_7_out), .gate(e));
  Transistor transistor_8 (.in(transistor_7_out), .out(transistor_8_out), .gate(f));
  Transistor #(.\type ("n")) transistor_9 (.in(1'b0), .out(transistor_8_out), .gate(d));
  Transistor #(.\type ("n")) transistor_10 (.in(1'b0), .out(transistor_8_out), .gate(e));
  Transistor #(.\type ("n")) transistor_11 (.in(1'b0), .out(transistor_3_out), .gate(c));
  Transistor transistor_12 (.in(1'b1), .out(transistor_12_out), .gate(transistor_3_out));
  Transistor #(.\type ("n")) transistor_13 (.in(1'b0), .out(transistor_8_out), .gate(f));
  Transistor transistor_14 (.in(1'b1), .out(transistor_12_out), .gate(transistor_8_out));
  Transistor #(.\type ("n")) transistor_15 (.in(transistor_16_out), .out(transistor_12_out), .gate(transistor_3_out));
  Transistor #(.\type ("n")) transistor_16 (.in(1'b0), .out(transistor_16_out), .gate(transistor_8_out));
  Transistor transistor_17 (.in(1'b1), .out(g), .gate(transistor_12_out));
  Transistor #(.\type ("n")) transistor_18 (.in(1'b0), .out(g), .gate(transistor_12_out));
endmodule

module cell40 (
  input  b,
  input  c,
  input  d,
  input  e,
  input  f,
  output a
);

  wire transistor_1_out, transistor_4_out, transistor_5_out, transistor_8_out, transistor_9_out,
       transistor_11_out;

  Transistor transistor_1 (.in(1'b1), .out(transistor_1_out), .gate(b));
  Transistor transistor_2 (.in(1'b1), .out(transistor_1_out), .gate(c));
  Transistor #(.\type ("n")) transistor_3 (.in(transistor_4_out), .out(transistor_1_out), .gate(b));
  Transistor #(.\type ("n")) transistor_4 (.in(1'b0), .out(transistor_4_out), .gate(c));
  Transistor transistor_5 (.in(1'b1), .out(transistor_5_out), .gate(e));
  Transistor transistor_6 (.in(1'b1), .out(transistor_5_out), .gate(f));
  Transistor #(.\type ("n")) transistor_7 (.in(transistor_8_out), .out(transistor_5_out), .gate(d));
  Transistor #(.\type ("n")) transistor_8 (.in(transistor_9_out), .out(transistor_8_out), .gate(e));
  Transistor #(.\type ("n")) transistor_9 (.in(1'b0), .out(transistor_9_out), .gate(f));
  Transistor transistor_10 (.in(1'b1), .out(transistor_5_out), .gate(d));
  Transistor transistor_11 (.in(1'b1), .out(transistor_11_out), .gate(transistor_5_out));
  Transistor transistor_12 (.in(transistor_11_out), .out(a), .gate(transistor_1_out));
  Transistor #(.\type ("n")) transistor_13 (.in(1'b0), .out(a), .gate(transistor_5_out));
  Transistor #(.\type ("n")) transistor_14 (.in(1'b0), .out(a), .gate(transistor_1_out));
endmodule

module cell41 (
  input  a,
  input  b,
  input  c,
  input  d,
  output e
);

  wire transistor_1_out, transistor_2_out, transistor_3_out, transistor_4_out;

  Transistor transistor_1 (.in(1'b1), .out(transistor_1_out), .gate(a));
  Transistor transistor_2 (.in(transistor_1_out), .out(transistor_2_out), .gate(b));
  Transistor transistor_3 (.in(transistor_2_out), .out(transistor_3_out), .gate(c));
  Transistor transistor_4 (.in(transistor_3_out), .out(transistor_4_out), .gate(d));
  Transistor #(.\type ("n")) transistor_5 (.in(1'b0), .out(transistor_4_out), .gate(a));
  Transistor #(.\type ("n")) transistor_6 (.in(1'b0), .out(transistor_4_out), .gate(b));
  Transistor #(.\type ("n")) transistor_7 (.in(1'b0), .out(transistor_4_out), .gate(d));
  Transistor #(.\type ("n")) transistor_8 (.in(1'b0), .out(transistor_4_out), .gate(c));
  Transistor transistor_9 (.in(1'b1), .out(e), .gate(transistor_4_out));
  Transistor #(.\type ("n")) transistor_10 (.in(1'b0), .out(e), .gate(transistor_4_out));
endmodule

module cell42 (
  input  a,
  input  b,
  input  c,
  input  d,
  output e
);

  wire transistor_1_out, transistor_4_out, transistor_5_out, transistor_6_out;

  Transistor transistor_1 (.in(1'b1), .out(transistor_1_out), .gate(d));
  Transistor transistor_2 (.in(1'b1), .out(transistor_1_out), .gate(c));
  Transistor #(.\type ("n")) transistor_3 (.in(transistor_4_out), .out(transistor_1_out), .gate(a));
  Transistor #(.\type ("n")) transistor_4 (.in(transistor_5_out), .out(transistor_4_out), .gate(b));
  Transistor #(.\type ("n")) transistor_5 (.in(transistor_6_out), .out(transistor_5_out), .gate(c));
  Transistor #(.\type ("n")) transistor_6 (.in(1'b0), .out(transistor_6_out), .gate(d));
  Transistor transistor_7 (.in(1'b1), .out(transistor_1_out), .gate(a));
  Transistor transistor_8 (.in(1'b1), .out(transistor_1_out), .gate(b));
  Transistor transistor_9 (.in(1'b1), .out(e), .gate(transistor_1_out));
  Transistor #(.\type ("n")) transistor_10 (.in(1'b0), .out(e), .gate(transistor_1_out));
endmodule

module cell43 (
  input  c,
  input  b,
  input  d,
  input  e,
  output a
);

  wire transistor_1_out, transistor_4_out, transistor_8_out;

  Transistor transistor_1 (.in(1'b1), .out(transistor_1_out), .gate(b));
  Transistor transistor_2 (.in(transistor_1_out), .out(a), .gate(d));
  Transistor #(.\type ("n")) transistor_3 (.in(transistor_4_out), .out(a), .gate(c));
  Transistor #(.\type ("n")) transistor_4 (.in(1'b0), .out(transistor_4_out), .gate(b));
  Transistor transistor_5 (.in(1'b1), .out(transistor_1_out), .gate(c));
  Transistor transistor_6 (.in(transistor_1_out), .out(a), .gate(e));
  Transistor #(.\type ("n")) transistor_7 (.in(transistor_8_out), .out(a), .gate(d));
  Transistor #(.\type ("n")) transistor_8 (.in(1'b0), .out(transistor_8_out), .gate(e));
endmodule

module cell44 (
  input  b,
  input  c,
  input  d,
  input  e,
  input  f,
  input  g,
  input  h,
  input  i,
  output a
);

  wire transistor_2_out, transistor_3_out, transistor_5_out, transistor_7_out, transistor_13_out,
       transistor_14_out, transistor_16_out;

  Transistor #(.\type ("n")) transistor_1 (.in(transistor_2_out), .out(a), .gate(c));
  Transistor #(.\type ("n")) transistor_2 (.in(1'b0), .out(transistor_2_out), .gate(b));
  Transistor transistor_3 (.in(1'b1), .out(transistor_3_out), .gate(i));
  Transistor transistor_4 (.in(1'b1), .out(transistor_3_out), .gate(h));
  Transistor transistor_5 (.in(transistor_3_out), .out(transistor_5_out), .gate(g));
  Transistor transistor_6 (.in(transistor_3_out), .out(transistor_5_out), .gate(f));
  Transistor transistor_7 (.in(transistor_5_out), .out(transistor_7_out), .gate(e));
  Transistor transistor_8 (.in(transistor_5_out), .out(transistor_7_out), .gate(d));
  Transistor transistor_9 (.in(transistor_7_out), .out(a), .gate(c));
  Transistor transistor_10 (.in(transistor_7_out), .out(a), .gate(b));
  Transistor #(.\type ("n")) transistor_11 (.in(transistor_14_out), .out(a), .gate(g));
  Transistor #(.\type ("n")) transistor_12 (.in(transistor_13_out), .out(a), .gate(d));
  Transistor #(.\type ("n")) transistor_13 (.in(1'b0), .out(transistor_13_out), .gate(e));
  Transistor #(.\type ("n")) transistor_14 (.in(1'b0), .out(transistor_14_out), .gate(f));
  Transistor #(.\type ("n")) transistor_15 (.in(transistor_16_out), .out(a), .gate(h));
  Transistor #(.\type ("n")) transistor_16 (.in(1'b0), .out(transistor_16_out), .gate(i));
endmodule

module cell45 (
  input  na,
  input  b,
  input  a,
  output c
);

  wire transistor_1_out, transistor_3_out, transistor_5_out;

  Transistor transistor_1 (.in(1'b1), .out(transistor_1_out), .gate(b));
  Transistor #(.\type ("n")) transistor_2 (.in(1'b0), .out(transistor_1_out), .gate(b));
  Transistor transistor_3 (.in(b), .out(transistor_3_out), .gate(na));
  Transistor #(.\type ("n")) transistor_4 (.in(b), .out(transistor_3_out), .gate(a));
  Transistor transistor_5 (.in(1'b1), .out(transistor_5_out), .gate(transistor_3_out));
  Transistor transistor_6 (.in(transistor_5_out), .out(c), .gate(transistor_1_out));
  Transistor #(.\type ("n")) transistor_7 (.in(1'b0), .out(c), .gate(transistor_1_out));
  Transistor #(.\type ("n")) transistor_8 (.in(1'b0), .out(c), .gate(transistor_3_out));
endmodule

module cell46 (
  input  a,
  input  b,
  input  c,
  input  d,
  input  e,
  input  f,
  input  g,
  output h
);

  wire transistor_1_out, transistor_4_out, transistor_5_out, transistor_6_out, transistor_9_out,
       transistor_10_out, transistor_11_out, transistor_15_out;

  Transistor transistor_1 (.in(1'b1), .out(transistor_1_out), .gate(c));
  Transistor transistor_2 (.in(1'b1), .out(transistor_1_out), .gate(b));
  Transistor #(.\type ("n")) transistor_3 (.in(transistor_4_out), .out(transistor_1_out), .gate(a));
  Transistor #(.\type ("n")) transistor_4 (.in(transistor_5_out), .out(transistor_4_out), .gate(b));
  Transistor #(.\type ("n")) transistor_5 (.in(1'b0), .out(transistor_5_out), .gate(c));
  Transistor transistor_6 (.in(1'b1), .out(transistor_6_out), .gate(f));
  Transistor transistor_7 (.in(1'b1), .out(transistor_6_out), .gate(g));
  Transistor #(.\type ("n")) transistor_8 (.in(transistor_9_out), .out(transistor_6_out), .gate(d));
  Transistor #(.\type ("n")) transistor_9 (.in(transistor_10_out), .out(transistor_9_out), .gate(e));
  Transistor #(.\type ("n")) transistor_10 (.in(transistor_11_out), .out(transistor_10_out), .gate(f));
  Transistor #(.\type ("n")) transistor_11 (.in(1'b0), .out(transistor_11_out), .gate(g));
  Transistor transistor_12 (.in(1'b1), .out(transistor_1_out), .gate(a));
  Transistor transistor_13 (.in(1'b1), .out(transistor_6_out), .gate(e));
  Transistor transistor_14 (.in(1'b1), .out(transistor_6_out), .gate(d));
  Transistor transistor_15 (.in(1'b1), .out(transistor_15_out), .gate(transistor_6_out));
  Transistor transistor_16 (.in(transistor_15_out), .out(h), .gate(transistor_1_out));
  Transistor #(.\type ("n")) transistor_17 (.in(1'b0), .out(h), .gate(transistor_6_out));
  Transistor #(.\type ("n")) transistor_18 (.in(1'b0), .out(h), .gate(transistor_1_out));
endmodule

module cell47 (
  input  a,
  input  b,
  input  c,
  input  d,
  input  e,
  input  f,
  output g
);

  wire transistor_1_out, transistor_4_out, transistor_5_out, transistor_6_out, transistor_9_out,
       transistor_10_out, transistor_13_out;

  Transistor transistor_1 (.in(1'b1), .out(transistor_1_out), .gate(b));
  Transistor transistor_2 (.in(1'b1), .out(transistor_1_out), .gate(c));
  Transistor #(.\type ("n")) transistor_3 (.in(transistor_4_out), .out(transistor_1_out), .gate(a));
  Transistor #(.\type ("n")) transistor_4 (.in(transistor_5_out), .out(transistor_4_out), .gate(b));
  Transistor #(.\type ("n")) transistor_5 (.in(1'b0), .out(transistor_5_out), .gate(c));
  Transistor transistor_6 (.in(1'b1), .out(transistor_6_out), .gate(e));
  Transistor transistor_7 (.in(1'b1), .out(transistor_6_out), .gate(f));
  Transistor #(.\type ("n")) transistor_8 (.in(transistor_9_out), .out(transistor_6_out), .gate(d));
  Transistor #(.\type ("n")) transistor_9 (.in(transistor_10_out), .out(transistor_9_out), .gate(e));
  Transistor #(.\type ("n")) transistor_10 (.in(1'b0), .out(transistor_10_out), .gate(f));
  Transistor transistor_11 (.in(1'b1), .out(transistor_1_out), .gate(a));
  Transistor transistor_12 (.in(1'b1), .out(transistor_6_out), .gate(d));
  Transistor transistor_13 (.in(1'b1), .out(transistor_13_out), .gate(transistor_6_out));
  Transistor transistor_14 (.in(transistor_13_out), .out(g), .gate(transistor_1_out));
  Transistor #(.\type ("n")) transistor_15 (.in(1'b0), .out(g), .gate(transistor_1_out));
  Transistor #(.\type ("n")) transistor_16 (.in(1'b0), .out(g), .gate(transistor_6_out));
endmodule

module cell48 (
  input  a,
  input  b,
  input  c,
  input  d,
  input  e,
  output f
);

  wire transistor_1_out, transistor_2_out, transistor_3_out, transistor_6_out, transistor_7_out,
       transistor_11_out, transistor_13_out;

  Transistor transistor_1 (.in(1'b1), .out(transistor_1_out), .gate(a));
  Transistor transistor_2 (.in(transistor_1_out), .out(transistor_2_out), .gate(b));
  Transistor transistor_3 (.in(transistor_2_out), .out(transistor_3_out), .gate(c));
  Transistor #(.\type ("n")) transistor_4 (.in(1'b0), .out(transistor_3_out), .gate(b));
  Transistor #(.\type ("n")) transistor_5 (.in(1'b0), .out(transistor_3_out), .gate(a));
  Transistor transistor_6 (.in(1'b1), .out(transistor_6_out), .gate(d));
  Transistor transistor_7 (.in(transistor_6_out), .out(transistor_7_out), .gate(e));
  Transistor #(.\type ("n")) transistor_8 (.in(1'b0), .out(transistor_7_out), .gate(e));
  Transistor #(.\type ("n")) transistor_9 (.in(1'b0), .out(transistor_7_out), .gate(d));
  Transistor #(.\type ("n")) transistor_10 (.in(1'b0), .out(transistor_3_out), .gate(c));
  Transistor transistor_11 (.in(1'b1), .out(transistor_11_out), .gate(transistor_3_out));
  Transistor #(.\type ("n")) transistor_12 (.in(transistor_13_out), .out(transistor_11_out), .gate(transistor_7_out));
  Transistor #(.\type ("n")) transistor_13 (.in(1'b0), .out(transistor_13_out), .gate(transistor_3_out));
  Transistor transistor_14 (.in(1'b1), .out(transistor_11_out), .gate(transistor_7_out));
  Transistor transistor_15 (.in(1'b1), .out(f), .gate(transistor_11_out));
  Transistor #(.\type ("n")) transistor_16 (.in(1'b0), .out(f), .gate(transistor_11_out));
endmodule

module cell49 (
  input  b,
  input  c,
  output a
);

  wire transistor_1_out, transistor_3_out, transistor_4_out, transistor_7_out, transistor_8_out;

  Transistor transistor_1 (.in(1'b1), .out(transistor_1_out), .gate(c));
  Transistor #(.\type ("n")) transistor_2 (.in(transistor_3_out), .out(transistor_1_out), .gate(c));
  Transistor #(.\type ("n")) transistor_3 (.in(1'b0), .out(transistor_3_out), .gate(b));
  Transistor transistor_4 (.in(1'b1), .out(transistor_4_out), .gate(c));
  Transistor #(.\type ("n")) transistor_5 (.in(1'b0), .out(transistor_4_out), .gate(c));
  Transistor transistor_6 (.in(1'b1), .out(transistor_1_out), .gate(b));
  Transistor transistor_7 (.in(1'b1), .out(transistor_7_out), .gate(b));
  Transistor transistor_8 (.in(transistor_7_out), .out(transistor_8_out), .gate(transistor_4_out));
  Transistor #(.\type ("n")) transistor_9 (.in(1'b0), .out(transistor_8_out), .gate(b));
  Transistor #(.\type ("n")) transistor_10 (.in(1'b0), .out(transistor_8_out), .gate(transistor_4_out));
  Transistor transistor_11 (.in(1'b1), .out(a), .gate(transistor_1_out));
  Transistor transistor_12 (.in(1'b1), .out(a), .gate(transistor_1_out));
  Transistor #(.\type ("n")) transistor_13 (.in(1'b0), .out(a), .gate(transistor_8_out));
  Transistor #(.\type ("n")) transistor_14 (.in(1'b0), .out(a), .gate(transistor_8_out));
endmodule

module cell50 (
  input  in_1
);

  wire transistor_1_out, undriven;

  Transistor #(.\type ("n")) transistor_1 (.in(undriven), .out(transistor_1_out), .gate(in_1));
  // also tied to GND on the sheet: transistor_1_out
endmodule

module cell51 (
  input  b,
  input  c,
  input  d,
  input  e,
  input  f,
  output a
);

  wire transistor_1_out, transistor_3_out, transistor_5_out, transistor_6_out, transistor_10_out;

  Transistor transistor_1 (.in(1'b1), .out(transistor_1_out), .gate(c));
  Transistor transistor_2 (.in(1'b1), .out(transistor_1_out), .gate(b));
  Transistor transistor_3 (.in(transistor_1_out), .out(transistor_3_out), .gate(e));
  Transistor #(.\type ("n")) transistor_4 (.in(transistor_5_out), .out(transistor_3_out), .gate(d));
  Transistor #(.\type ("n")) transistor_5 (.in(transistor_6_out), .out(transistor_5_out), .gate(c));
  Transistor #(.\type ("n")) transistor_6 (.in(1'b0), .out(transistor_6_out), .gate(b));
  Transistor transistor_7 (.in(1'b1), .out(transistor_1_out), .gate(d));
  Transistor transistor_8 (.in(transistor_1_out), .out(transistor_3_out), .gate(f));
  Transistor #(.\type ("n")) transistor_9 (.in(transistor_10_out), .out(transistor_3_out), .gate(e));
  Transistor #(.\type ("n")) transistor_10 (.in(1'b0), .out(transistor_10_out), .gate(f));
  Transistor transistor_11 (.in(1'b1), .out(a), .gate(transistor_3_out));
  Transistor #(.\type ("n")) transistor_12 (.in(1'b0), .out(a), .gate(transistor_3_out));
endmodule

module cell72 (
  input  clk,
  input  r,
  input  d_in,
  output d_out
);

  wire transistor_1_out, transistor_3_out, transistor_5_out, transistor_7_out, transistor_9_out,
       transistor_10_out, transistor_12_out, transistor_13_out, transistor_16_out, transistor_17_out,
       transistor_19_out, transistor_21_out, transistor_23_out, transistor_24_out, transistor_26_out,
       transistor_27_out, transistor_30_out, transistor_31_out, transistor_34_out;

  Transistor transistor_1 (.in(1'b1), .out(transistor_1_out), .gate(clk));
  Transistor #(.\type ("n")) transistor_2 (.in(1'b0), .out(transistor_1_out), .gate(clk));
  Transistor transistor_3 (.in(1'b1), .out(transistor_3_out), .gate(clk));
  Transistor #(.\type ("n")) transistor_4 (.in(1'b0), .out(transistor_3_out), .gate(clk));
  Transistor transistor_5 (.in(1'b1), .out(transistor_5_out), .gate(transistor_3_out));
  Transistor #(.\type ("n")) transistor_6 (.in(1'b0), .out(transistor_5_out), .gate(transistor_3_out));
  Transistor transistor_7 (.in(1'b1), .out(transistor_7_out), .gate(d_in));
  Transistor #(.\type ("n")) transistor_8 (.in(1'b0), .out(transistor_7_out), .gate(d_in));
  Transistor transistor_9 (.in(1'b1), .out(transistor_9_out), .gate(transistor_7_out));
  Transistor transistor_10 (.in(transistor_9_out), .out(transistor_10_out), .gate(transistor_5_out));
  Transistor #(.\type ("n")) transistor_11 (.in(transistor_12_out), .out(transistor_10_out), .gate(transistor_7_out));
  Transistor #(.\type ("n")) transistor_12 (.in(1'b0), .out(transistor_12_out), .gate(transistor_1_out));
  Transistor transistor_13 (.in(1'b1), .out(transistor_13_out), .gate(transistor_19_out));
  Transistor transistor_14 (.in(transistor_13_out), .out(transistor_10_out), .gate(transistor_1_out));
  Transistor #(.\type ("n")) transistor_15 (.in(transistor_16_out), .out(transistor_10_out), .gate(transistor_5_out));
  Transistor #(.\type ("n")) transistor_16 (.in(1'b0), .out(transistor_16_out), .gate(transistor_19_out));
  Transistor transistor_17 (.in(1'b1), .out(transistor_17_out), .gate(r));
  Transistor #(.\type ("n")) transistor_18 (.in(1'b0), .out(transistor_17_out), .gate(r));
  Transistor transistor_19 (.in(1'b1), .out(transistor_19_out), .gate(transistor_10_out));
  Transistor #(.\type ("n")) transistor_20 (.in(transistor_21_out), .out(transistor_19_out), .gate(transistor_10_out));
  Transistor #(.\type ("n")) transistor_21 (.in(1'b0), .out(transistor_21_out), .gate(transistor_17_out));
  Transistor transistor_22 (.in(1'b1), .out(transistor_19_out), .gate(transistor_17_out));
  Transistor transistor_23 (.in(1'b1), .out(transistor_23_out), .gate(transistor_19_out));
  Transistor transistor_24 (.in(transistor_23_out), .out(transistor_24_out), .gate(transistor_1_out));
  Transistor #(.\type ("n")) transistor_25 (.in(transistor_26_out), .out(transistor_24_out), .gate(transistor_5_out));
  Transistor #(.\type ("n")) transistor_26 (.in(1'b0), .out(transistor_26_out), .gate(transistor_19_out));
  Transistor transistor_27 (.in(1'b1), .out(transistor_27_out), .gate(transistor_31_out));
  Transistor transistor_28 (.in(transistor_27_out), .out(transistor_24_out), .gate(transistor_5_out));
  Transistor #(.\type ("n")) transistor_29 (.in(transistor_30_out), .out(transistor_24_out), .gate(transistor_1_out));
  Transistor #(.\type ("n")) transistor_30 (.in(1'b0), .out(transistor_30_out), .gate(transistor_31_out));
  Transistor transistor_31 (.in(1'b1), .out(transistor_31_out), .gate(transistor_17_out));
  Transistor transistor_32 (.in(1'b1), .out(transistor_31_out), .gate(transistor_24_out));
  Transistor #(.\type ("n")) transistor_33 (.in(transistor_34_out), .out(transistor_31_out), .gate(transistor_24_out));
  Transistor #(.\type ("n")) transistor_34 (.in(1'b0), .out(transistor_34_out), .gate(transistor_17_out));
  Transistor transistor_35 (.in(1'b1), .out(d_out), .gate(transistor_31_out));
  Transistor #(.\type ("n")) transistor_36 (.in(1'b0), .out(d_out), .gate(transistor_31_out));
endmodule

module cell52 (
  input  nload,
  input  val,
  input  load,
  input  nc1,
  input  nc2,
  input  c_in,
  input  r,
  input  c2,
  input  c1,
  output c_out,
  output s
);

  wire transistor_1_out, transistor_4_out, transistor_7_out, transistor_8_out, transistor_9_out,
       transistor_11_out, transistor_12_out, transistor_16_out, transistor_17_out, transistor_19_out,
       transistor_20_out, transistor_22_out, transistor_25_out, transistor_26_out, transistor_27_out,
       transistor_31_out, transistor_32_out;

  Transistor transistor_1 (.in(1'b1), .out(transistor_1_out), .gate(c_in));
  Transistor #(.\type ("n")) transistor_2 (.in(1'b0), .out(transistor_1_out), .gate(c_in));
  Transistor #(.\type ("n")) transistor_3 (.in(1'b0), .out(c_out), .gate(transistor_1_out));
  Transistor transistor_4 (.in(1'b1), .out(transistor_4_out), .gate(transistor_27_out));
  Transistor transistor_5 (.in(transistor_4_out), .out(c_out), .gate(transistor_1_out));
  Transistor #(.\type ("n")) transistor_6 (.in(1'b0), .out(c_out), .gate(transistor_27_out));
  Transistor transistor_7 (.in(1'b1), .out(transistor_7_out), .gate(transistor_1_out));
  Transistor transistor_8 (.in(transistor_7_out), .out(transistor_8_out), .gate(c_out));
  Transistor transistor_9 (.in(transistor_8_out), .out(transistor_9_out), .gate(r));
  Transistor #(.\type ("n")) transistor_10 (.in(1'b0), .out(transistor_9_out), .gate(r));
  Transistor transistor_11 (.in(1'b1), .out(transistor_11_out), .gate(c_out));
  Transistor transistor_12 (.in(transistor_11_out), .out(transistor_12_out), .gate(transistor_27_out));
  Transistor transistor_13 (.in(transistor_12_out), .out(transistor_9_out), .gate(r));
  Transistor #(.\type ("n")) transistor_14 (.in(1'b0), .out(transistor_9_out), .gate(c_out));
  Transistor #(.\type ("n")) transistor_15 (.in(transistor_16_out), .out(transistor_9_out), .gate(transistor_27_out));
  Transistor #(.\type ("n")) transistor_16 (.in(1'b0), .out(transistor_16_out), .gate(transistor_1_out));
  Transistor transistor_17 (.in(transistor_9_out), .out(transistor_17_out), .gate(nc1));
  Transistor #(.\type ("n")) transistor_18 (.in(transistor_9_out), .out(transistor_17_out), .gate(c1));
  Transistor transistor_19 (.in(1'b1), .out(transistor_19_out), .gate(transistor_17_out));
  Transistor transistor_20 (.in(transistor_19_out), .out(transistor_20_out), .gate(nc2));
  Transistor #(.\type ("n")) transistor_21 (.in(transistor_22_out), .out(transistor_20_out), .gate(c2));
  Transistor #(.\type ("n")) transistor_22 (.in(1'b0), .out(transistor_22_out), .gate(transistor_17_out));
  Transistor transistor_23 (.in(1'b1), .out(s), .gate(transistor_20_out));
  Transistor #(.\type ("n")) transistor_24 (.in(1'b0), .out(s), .gate(transistor_20_out));
  Transistor transistor_25 (.in(1'b1), .out(transistor_25_out), .gate(val));
  Transistor transistor_26 (.in(1'b1), .out(transistor_26_out), .gate(s));
  Transistor transistor_27 (.in(transistor_26_out), .out(transistor_27_out), .gate(load));
  Transistor transistor_28 (.in(transistor_25_out), .out(transistor_27_out), .gate(nload));
  Transistor #(.\type ("n")) transistor_29 (.in(transistor_32_out), .out(transistor_27_out), .gate(load));
  Transistor #(.\type ("n")) transistor_30 (.in(transistor_31_out), .out(transistor_27_out), .gate(nload));
  Transistor #(.\type ("n")) transistor_31 (.in(1'b0), .out(transistor_31_out), .gate(s));
  Transistor #(.\type ("n")) transistor_32 (.in(1'b0), .out(transistor_32_out), .gate(val));
endmodule

module cell53 (
  input  a,
  input  b,
  input  c,
  input  d,
  input  e,
  input  f,
  output g
);

  wire transistor_1_out, transistor_2_out, transistor_3_out, transistor_5_out, transistor_11_out,
       transistor_12_out;

  Transistor transistor_1 (.in(1'b1), .out(transistor_1_out), .gate(b));
  Transistor transistor_2 (.in(transistor_1_out), .out(transistor_2_out), .gate(c));
  Transistor transistor_3 (.in(transistor_2_out), .out(transistor_3_out), .gate(e));
  Transistor #(.\type ("n")) transistor_4 (.in(transistor_5_out), .out(transistor_3_out), .gate(a));
  Transistor #(.\type ("n")) transistor_5 (.in(1'b0), .out(transistor_5_out), .gate(b));
  Transistor transistor_6 (.in(1'b1), .out(transistor_1_out), .gate(a));
  Transistor transistor_7 (.in(transistor_1_out), .out(transistor_2_out), .gate(d));
  Transistor transistor_8 (.in(transistor_2_out), .out(transistor_3_out), .gate(f));
  Transistor #(.\type ("n")) transistor_9 (.in(transistor_11_out), .out(transistor_3_out), .gate(e));
  Transistor #(.\type ("n")) transistor_10 (.in(transistor_12_out), .out(transistor_3_out), .gate(d));
  Transistor #(.\type ("n")) transistor_11 (.in(1'b0), .out(transistor_11_out), .gate(f));
  Transistor #(.\type ("n")) transistor_12 (.in(1'b0), .out(transistor_12_out), .gate(c));
  Transistor transistor_13 (.in(1'b1), .out(g), .gate(transistor_3_out));
  Transistor #(.\type ("n")) transistor_14 (.in(1'b0), .out(g), .gate(transistor_3_out));
endmodule

module cell54 (
  input  a,
  input  b,
  input  c,
  input  d,
  input  e,
  input  f,
  input  h,
  input  i,
  input  j,
  input  k,
  input  l,
  input  m,
  output g
);

  wire transistor_1_out, transistor_2_out, transistor_3_out, transistor_5_out, transistor_6_out,
       transistor_7_out, transistor_8_out, transistor_10_out, transistor_16_out, transistor_17_out,
       transistor_23_out, transistor_24_out, transistor_25_out, transistor_28_out;

  Transistor transistor_1 (.in(1'b1), .out(transistor_1_out), .gate(e));
  Transistor transistor_2 (.in(transistor_1_out), .out(transistor_2_out), .gate(d));
  Transistor transistor_3 (.in(transistor_2_out), .out(transistor_3_out), .gate(b));
  Transistor #(.\type ("n")) transistor_4 (.in(transistor_5_out), .out(transistor_3_out), .gate(f));
  Transistor #(.\type ("n")) transistor_5 (.in(1'b0), .out(transistor_5_out), .gate(e));
  Transistor transistor_6 (.in(1'b1), .out(transistor_6_out), .gate(i));
  Transistor transistor_7 (.in(transistor_6_out), .out(transistor_7_out), .gate(j));
  Transistor transistor_8 (.in(transistor_7_out), .out(transistor_8_out), .gate(l));
  Transistor #(.\type ("n")) transistor_9 (.in(transistor_10_out), .out(transistor_8_out), .gate(h));
  Transistor #(.\type ("n")) transistor_10 (.in(1'b0), .out(transistor_10_out), .gate(i));
  Transistor transistor_11 (.in(1'b1), .out(transistor_1_out), .gate(f));
  Transistor transistor_12 (.in(transistor_1_out), .out(transistor_2_out), .gate(c));
  Transistor transistor_13 (.in(transistor_2_out), .out(transistor_3_out), .gate(a));
  Transistor #(.\type ("n")) transistor_14 (.in(transistor_17_out), .out(transistor_3_out), .gate(b));
  Transistor #(.\type ("n")) transistor_15 (.in(transistor_16_out), .out(transistor_3_out), .gate(c));
  Transistor #(.\type ("n")) transistor_16 (.in(1'b0), .out(transistor_16_out), .gate(d));
  Transistor #(.\type ("n")) transistor_17 (.in(1'b0), .out(transistor_17_out), .gate(a));
  Transistor transistor_18 (.in(1'b1), .out(transistor_6_out), .gate(h));
  Transistor transistor_19 (.in(transistor_6_out), .out(transistor_7_out), .gate(k));
  Transistor transistor_20 (.in(transistor_7_out), .out(transistor_8_out), .gate(m));
  Transistor #(.\type ("n")) transistor_21 (.in(transistor_24_out), .out(transistor_8_out), .gate(k));
  Transistor #(.\type ("n")) transistor_22 (.in(transistor_23_out), .out(transistor_8_out), .gate(l));
  Transistor #(.\type ("n")) transistor_23 (.in(1'b0), .out(transistor_23_out), .gate(m));
  Transistor #(.\type ("n")) transistor_24 (.in(1'b0), .out(transistor_24_out), .gate(j));
  Transistor transistor_25 (.in(1'b1), .out(transistor_25_out), .gate(transistor_8_out));
  Transistor transistor_26 (.in(1'b1), .out(transistor_25_out), .gate(transistor_3_out));
  Transistor #(.\type ("n")) transistor_27 (.in(transistor_28_out), .out(transistor_25_out), .gate(transistor_3_out));
  Transistor #(.\type ("n")) transistor_28 (.in(1'b0), .out(transistor_28_out), .gate(transistor_8_out));
  Transistor transistor_29 (.in(1'b1), .out(g), .gate(transistor_25_out));
  Transistor #(.\type ("n")) transistor_30 (.in(1'b0), .out(g), .gate(transistor_25_out));
endmodule

module cell55 (
  input  b,
  input  j,
  input  c,
  input  k,
  input  d,
  input  l,
  input  e,
  input  m,
  input  f,
  input  n,
  input  g,
  input  o,
  input  h,
  input  p,
  input  i,
  input  q,
  output a
);

  wire transistor_1_out, transistor_2_out, transistor_3_out, transistor_5_out, transistor_7_out,
       transistor_13_out, transistor_14_out, transistor_16_out, transistor_17_out, transistor_18_out,
       transistor_19_out, transistor_20_out, transistor_21_out, transistor_24_out, transistor_30_out,
       transistor_32_out, transistor_36_out;

  Transistor #(.\type ("n")) transistor_1 (.in(transistor_2_out), .out(transistor_1_out), .gate(c));
  Transistor #(.\type ("n")) transistor_2 (.in(1'b0), .out(transistor_2_out), .gate(b));
  Transistor transistor_3 (.in(1'b1), .out(transistor_3_out), .gate(h));
  Transistor transistor_4 (.in(1'b1), .out(transistor_3_out), .gate(i));
  Transistor transistor_5 (.in(transistor_3_out), .out(transistor_5_out), .gate(f));
  Transistor transistor_6 (.in(transistor_3_out), .out(transistor_5_out), .gate(g));
  Transistor transistor_7 (.in(transistor_5_out), .out(transistor_7_out), .gate(d));
  Transistor transistor_8 (.in(transistor_5_out), .out(transistor_7_out), .gate(e));
  Transistor transistor_9 (.in(transistor_7_out), .out(transistor_1_out), .gate(b));
  Transistor transistor_10 (.in(transistor_7_out), .out(transistor_1_out), .gate(c));
  Transistor #(.\type ("n")) transistor_11 (.in(transistor_14_out), .out(transistor_1_out), .gate(d));
  Transistor #(.\type ("n")) transistor_12 (.in(transistor_13_out), .out(transistor_1_out), .gate(g));
  Transistor #(.\type ("n")) transistor_13 (.in(1'b0), .out(transistor_13_out), .gate(f));
  Transistor #(.\type ("n")) transistor_14 (.in(1'b0), .out(transistor_14_out), .gate(e));
  Transistor #(.\type ("n")) transistor_15 (.in(transistor_16_out), .out(transistor_1_out), .gate(h));
  Transistor #(.\type ("n")) transistor_16 (.in(1'b0), .out(transistor_16_out), .gate(i));
  Transistor #(.\type ("n")) transistor_17 (.in(transistor_18_out), .out(transistor_17_out), .gate(k));
  Transistor #(.\type ("n")) transistor_18 (.in(1'b0), .out(transistor_18_out), .gate(j));
  Transistor transistor_19 (.in(1'b1), .out(transistor_19_out), .gate(p));
  Transistor transistor_20 (.in(transistor_19_out), .out(transistor_20_out), .gate(n));
  Transistor transistor_21 (.in(transistor_20_out), .out(transistor_21_out), .gate(l));
  Transistor transistor_22 (.in(transistor_21_out), .out(transistor_17_out), .gate(j));
  Transistor #(.\type ("n")) transistor_23 (.in(transistor_24_out), .out(transistor_17_out), .gate(l));
  Transistor #(.\type ("n")) transistor_24 (.in(1'b0), .out(transistor_24_out), .gate(m));
  Transistor transistor_25 (.in(1'b1), .out(transistor_19_out), .gate(q));
  Transistor transistor_26 (.in(transistor_19_out), .out(transistor_20_out), .gate(o));
  Transistor transistor_27 (.in(transistor_20_out), .out(transistor_21_out), .gate(m));
  Transistor transistor_28 (.in(transistor_21_out), .out(transistor_17_out), .gate(k));
  Transistor #(.\type ("n")) transistor_29 (.in(transistor_30_out), .out(transistor_17_out), .gate(o));
  Transistor #(.\type ("n")) transistor_30 (.in(1'b0), .out(transistor_30_out), .gate(n));
  Transistor #(.\type ("n")) transistor_31 (.in(transistor_32_out), .out(transistor_17_out), .gate(p));
  Transistor #(.\type ("n")) transistor_32 (.in(1'b0), .out(transistor_32_out), .gate(q));
  Transistor transistor_33 (.in(1'b1), .out(a), .gate(transistor_1_out));
  Transistor transistor_34 (.in(1'b1), .out(a), .gate(transistor_17_out));
  Transistor #(.\type ("n")) transistor_35 (.in(transistor_36_out), .out(a), .gate(transistor_1_out));
  Transistor #(.\type ("n")) transistor_36 (.in(1'b0), .out(transistor_36_out), .gate(transistor_17_out));
endmodule

module cell56 (
  input  nc2,
  input  nc2_2,
  input  in_3,
  input  c1,
  input  c2,
  output out_6
);

  wire transistor_2_out, transistor_4_out, transistor_6_out, transistor_7_out, transistor_9_out;

  Transistor transistor_1 (.in(1'b1), .out(in_3), .gate(nc2_2));
  Transistor transistor_2 (.in(1'b1), .out(transistor_2_out), .gate(in_3));
  Transistor #(.\type ("n")) transistor_3 (.in(1'b0), .out(transistor_2_out), .gate(in_3));
  Transistor transistor_4 (.in(transistor_2_out), .out(transistor_4_out), .gate(nc2));
  Transistor #(.\type ("n")) transistor_5 (.in(transistor_2_out), .out(transistor_4_out), .gate(c1));
  Transistor transistor_6 (.in(1'b1), .out(transistor_6_out), .gate(transistor_4_out));
  Transistor transistor_7 (.in(transistor_6_out), .out(transistor_7_out), .gate(nc2_2));
  Transistor #(.\type ("n")) transistor_8 (.in(transistor_9_out), .out(transistor_7_out), .gate(c2));
  Transistor #(.\type ("n")) transistor_9 (.in(1'b0), .out(transistor_9_out), .gate(transistor_4_out));
  Transistor transistor_10 (.in(1'b1), .out(out_6), .gate(transistor_7_out));
  Transistor #(.\type ("n")) transistor_11 (.in(1'b0), .out(out_6), .gate(transistor_7_out));
endmodule

module cell57 (
  input  a,
  input  b,
  input  c,
  input  d,
  input  e,
  input  f,
  output g
);

  wire transistor_1_out, transistor_6_out, transistor_7_out, transistor_11_out, transistor_12_out;

  Transistor transistor_1 (.in(1'b1), .out(transistor_1_out), .gate(e));
  Transistor transistor_2 (.in(1'b1), .out(transistor_1_out), .gate(d));
  Transistor transistor_3 (.in(transistor_1_out), .out(g), .gate(a));
  Transistor transistor_4 (.in(transistor_1_out), .out(g), .gate(b));
  Transistor #(.\type ("n")) transistor_5 (.in(transistor_6_out), .out(g), .gate(c));
  Transistor #(.\type ("n")) transistor_6 (.in(transistor_7_out), .out(transistor_6_out), .gate(b));
  Transistor #(.\type ("n")) transistor_7 (.in(1'b0), .out(transistor_7_out), .gate(a));
  Transistor transistor_8 (.in(1'b1), .out(transistor_1_out), .gate(f));
  Transistor transistor_9 (.in(transistor_1_out), .out(g), .gate(c));
  Transistor #(.\type ("n")) transistor_10 (.in(transistor_11_out), .out(g), .gate(d));
  Transistor #(.\type ("n")) transistor_11 (.in(transistor_12_out), .out(transistor_11_out), .gate(e));
  Transistor #(.\type ("n")) transistor_12 (.in(1'b0), .out(transistor_12_out), .gate(f));
endmodule

module cell58 (
  input  a,
  input  b,
  input  c,
  input  d,
  input  e,
  input  f,
  input  g,
  input  h,
  input  i,
  output j
);

  wire transistor_1_out, transistor_2_out, transistor_5_out, transistor_6_out, transistor_11_out,
       transistor_12_out, transistor_17_out, transistor_18_out;

  Transistor transistor_1 (.in(1'b1), .out(transistor_1_out), .gate(a));
  Transistor transistor_2 (.in(transistor_1_out), .out(transistor_2_out), .gate(d));
  Transistor transistor_3 (.in(transistor_2_out), .out(j), .gate(g));
  Transistor #(.\type ("n")) transistor_4 (.in(transistor_5_out), .out(j), .gate(c));
  Transistor #(.\type ("n")) transistor_5 (.in(transistor_6_out), .out(transistor_5_out), .gate(b));
  Transistor #(.\type ("n")) transistor_6 (.in(1'b0), .out(transistor_6_out), .gate(a));
  Transistor transistor_7 (.in(1'b1), .out(transistor_1_out), .gate(b));
  Transistor transistor_8 (.in(transistor_1_out), .out(transistor_2_out), .gate(e));
  Transistor transistor_9 (.in(transistor_2_out), .out(j), .gate(h));
  Transistor #(.\type ("n")) transistor_10 (.in(transistor_11_out), .out(j), .gate(d));
  Transistor #(.\type ("n")) transistor_11 (.in(transistor_12_out), .out(transistor_11_out), .gate(e));
  Transistor #(.\type ("n")) transistor_12 (.in(1'b0), .out(transistor_12_out), .gate(f));
  Transistor transistor_13 (.in(1'b1), .out(transistor_1_out), .gate(c));
  Transistor transistor_14 (.in(transistor_1_out), .out(transistor_2_out), .gate(f));
  Transistor transistor_15 (.in(transistor_2_out), .out(j), .gate(i));
  Transistor #(.\type ("n")) transistor_16 (.in(transistor_17_out), .out(j), .gate(i));
  Transistor #(.\type ("n")) transistor_17 (.in(transistor_18_out), .out(transistor_17_out), .gate(h));
  Transistor #(.\type ("n")) transistor_18 (.in(1'b0), .out(transistor_18_out), .gate(g));
endmodule

module cell59 (
  input  a,
  input  b,
  input  c,
  input  d,
  input  e,
  input  f,
  input  g,
  input  h,
  input  i,
  input  j,
  input  k,
  input  l,
  output m
);

  wire transistor_1_out, transistor_2_out, transistor_3_out, transistor_4_out, transistor_5_out,
       transistor_6_out, transistor_9_out, transistor_10_out, transistor_20_out, transistor_21_out,
       transistor_25_out, transistor_26_out;

  Transistor #(.\type ("n")) transistor_1 (.in(transistor_2_out), .out(transistor_1_out), .gate(c));
  Transistor #(.\type ("n")) transistor_2 (.in(transistor_3_out), .out(transistor_2_out), .gate(b));
  Transistor #(.\type ("n")) transistor_3 (.in(1'b0), .out(transistor_3_out), .gate(a));
  Transistor transistor_4 (.in(1'b1), .out(transistor_4_out), .gate(c));
  Transistor transistor_5 (.in(transistor_4_out), .out(transistor_5_out), .gate(f));
  Transistor transistor_6 (.in(transistor_5_out), .out(transistor_6_out), .gate(i));
  Transistor transistor_7 (.in(transistor_6_out), .out(transistor_1_out), .gate(l));
  Transistor #(.\type ("n")) transistor_8 (.in(transistor_9_out), .out(transistor_1_out), .gate(d));
  Transistor #(.\type ("n")) transistor_9 (.in(transistor_10_out), .out(transistor_9_out), .gate(e));
  Transistor #(.\type ("n")) transistor_10 (.in(1'b0), .out(transistor_10_out), .gate(f));
  Transistor transistor_11 (.in(1'b1), .out(transistor_4_out), .gate(a));
  Transistor transistor_12 (.in(1'b1), .out(transistor_4_out), .gate(b));
  Transistor transistor_13 (.in(transistor_4_out), .out(transistor_5_out), .gate(d));
  Transistor transistor_14 (.in(transistor_4_out), .out(transistor_5_out), .gate(e));
  Transistor transistor_15 (.in(transistor_5_out), .out(transistor_6_out), .gate(h));
  Transistor transistor_16 (.in(transistor_5_out), .out(transistor_6_out), .gate(g));
  Transistor transistor_17 (.in(transistor_6_out), .out(transistor_1_out), .gate(k));
  Transistor transistor_18 (.in(transistor_6_out), .out(transistor_1_out), .gate(j));
  Transistor #(.\type ("n")) transistor_19 (.in(transistor_20_out), .out(transistor_1_out), .gate(i));
  Transistor #(.\type ("n")) transistor_20 (.in(transistor_21_out), .out(transistor_20_out), .gate(h));
  Transistor #(.\type ("n")) transistor_21 (.in(1'b0), .out(transistor_21_out), .gate(g));
  Transistor transistor_22 (.in(1'b1), .out(m), .gate(transistor_1_out));
  Transistor #(.\type ("n")) transistor_23 (.in(1'b0), .out(m), .gate(transistor_1_out));
  Transistor #(.\type ("n")) transistor_24 (.in(transistor_25_out), .out(transistor_1_out), .gate(j));
  Transistor #(.\type ("n")) transistor_25 (.in(transistor_26_out), .out(transistor_25_out), .gate(k));
  Transistor #(.\type ("n")) transistor_26 (.in(1'b0), .out(transistor_26_out), .gate(l));
endmodule

module cell60 (
  input  nc1,
  input  a,
  input  c1,
  output b
);

  wire transistor_1_out;

  Transistor transistor_1 (.in(a), .out(transistor_1_out), .gate(nc1));
  Transistor #(.\type ("n")) transistor_2 (.in(a), .out(transistor_1_out), .gate(c1));
  Transistor transistor_3 (.in(1'b1), .out(b), .gate(transistor_1_out));
  Transistor #(.\type ("n")) transistor_4 (.in(1'b0), .out(b), .gate(transistor_1_out));
  Transistor transistor_5 (.in(1'b1), .out(b), .gate(transistor_1_out));
  Transistor #(.\type ("n")) transistor_6 (.in(1'b0), .out(b), .gate(transistor_1_out));
endmodule

module cell61 (
  input  nc1,
  input  nc2,
  input  a,
  input  b,
  input  c,
  input  c1,
  input  c2,
  output d
);

  wire transistor_1_out, transistor_2_out, transistor_4_out, transistor_7_out, transistor_8_out,
       transistor_10_out, transistor_11_out, transistor_12_out, transistor_14_out;

  Transistor transistor_1 (.in(1'b1), .out(transistor_1_out), .gate(a));
  Transistor transistor_2 (.in(transistor_1_out), .out(transistor_2_out), .gate(c));
  Transistor #(.\type ("n")) transistor_3 (.in(transistor_4_out), .out(transistor_2_out), .gate(b));
  Transistor #(.\type ("n")) transistor_4 (.in(1'b0), .out(transistor_4_out), .gate(a));
  Transistor transistor_5 (.in(1'b1), .out(transistor_1_out), .gate(b));
  Transistor #(.\type ("n")) transistor_6 (.in(1'b0), .out(transistor_2_out), .gate(c));
  Transistor transistor_7 (.in(1'b1), .out(transistor_7_out), .gate(transistor_2_out));
  Transistor transistor_8 (.in(transistor_7_out), .out(transistor_8_out), .gate(nc1));
  Transistor #(.\type ("n")) transistor_9 (.in(transistor_10_out), .out(transistor_8_out), .gate(c1));
  Transistor #(.\type ("n")) transistor_10 (.in(1'b0), .out(transistor_10_out), .gate(transistor_2_out));
  Transistor transistor_11 (.in(1'b1), .out(transistor_11_out), .gate(transistor_8_out));
  Transistor transistor_12 (.in(transistor_11_out), .out(transistor_12_out), .gate(nc2));
  Transistor #(.\type ("n")) transistor_13 (.in(transistor_14_out), .out(transistor_12_out), .gate(c2));
  Transistor #(.\type ("n")) transistor_14 (.in(1'b0), .out(transistor_14_out), .gate(transistor_8_out));
  Transistor transistor_15 (.in(1'b1), .out(d), .gate(transistor_12_out));
  Transistor #(.\type ("n")) transistor_16 (.in(1'b0), .out(d), .gate(transistor_12_out));
endmodule

module cell62 (
  input  b,
  input  c,
  input  d,
  input  e,
  input  f,
  output a
);

  wire transistor_2_out, transistor_4_out, transistor_8_out, transistor_10_out;

  Transistor #(.\type ("n")) transistor_1 (.in(1'b0), .out(a), .gate(b));
  Transistor transistor_2 (.in(1'b1), .out(transistor_2_out), .gate(d));
  Transistor transistor_3 (.in(1'b1), .out(transistor_2_out), .gate(c));
  Transistor transistor_4 (.in(transistor_2_out), .out(transistor_4_out), .gate(e));
  Transistor transistor_5 (.in(transistor_2_out), .out(transistor_4_out), .gate(f));
  Transistor transistor_6 (.in(transistor_4_out), .out(a), .gate(b));
  Transistor #(.\type ("n")) transistor_7 (.in(transistor_8_out), .out(a), .gate(c));
  Transistor #(.\type ("n")) transistor_8 (.in(1'b0), .out(transistor_8_out), .gate(d));
  Transistor #(.\type ("n")) transistor_9 (.in(transistor_10_out), .out(a), .gate(f));
  Transistor #(.\type ("n")) transistor_10 (.in(1'b0), .out(transistor_10_out), .gate(e));
endmodule

module cell63 (
  input  a,
  input  b,
  input  c,
  input  d,
  input  e,
  output f
);

  wire transistor_1_out, transistor_4_out, transistor_5_out, transistor_6_out, transistor_9_out,
       transistor_11_out, transistor_12_out;

  Transistor transistor_1 (.in(1'b1), .out(transistor_1_out), .gate(c));
  Transistor transistor_2 (.in(1'b1), .out(transistor_1_out), .gate(b));
  Transistor #(.\type ("n")) transistor_3 (.in(transistor_4_out), .out(transistor_1_out), .gate(a));
  Transistor #(.\type ("n")) transistor_4 (.in(transistor_5_out), .out(transistor_4_out), .gate(b));
  Transistor #(.\type ("n")) transistor_5 (.in(1'b0), .out(transistor_5_out), .gate(c));
  Transistor transistor_6 (.in(1'b1), .out(transistor_6_out), .gate(d));
  Transistor transistor_7 (.in(1'b1), .out(transistor_6_out), .gate(e));
  Transistor #(.\type ("n")) transistor_8 (.in(transistor_9_out), .out(transistor_6_out), .gate(d));
  Transistor #(.\type ("n")) transistor_9 (.in(1'b0), .out(transistor_9_out), .gate(e));
  Transistor transistor_10 (.in(1'b1), .out(transistor_1_out), .gate(a));
  Transistor #(.\type ("n")) transistor_11 (.in(1'b0), .out(transistor_11_out), .gate(transistor_6_out));
  Transistor transistor_12 (.in(1'b1), .out(transistor_12_out), .gate(transistor_6_out));
  Transistor transistor_13 (.in(transistor_12_out), .out(transistor_11_out), .gate(transistor_1_out));
  Transistor #(.\type ("n")) transistor_14 (.in(1'b0), .out(transistor_11_out), .gate(transistor_1_out));
  Transistor transistor_15 (.in(1'b1), .out(f), .gate(transistor_11_out));
  Transistor #(.\type ("n")) transistor_16 (.in(1'b0), .out(f), .gate(transistor_11_out));
endmodule

module cell64 (
  input  a,
  input  b,
  input  c,
  input  d,
  input  e,
  input  f,
  output g
);

  wire transistor_1_out, transistor_3_out, transistor_6_out, transistor_7_out, transistor_11_out,
       transistor_12_out;

  Transistor transistor_1 (.in(1'b1), .out(transistor_1_out), .gate(d));
  Transistor transistor_2 (.in(1'b1), .out(transistor_1_out), .gate(e));
  Transistor transistor_3 (.in(transistor_1_out), .out(transistor_3_out), .gate(a));
  Transistor transistor_4 (.in(transistor_1_out), .out(transistor_3_out), .gate(b));
  Transistor #(.\type ("n")) transistor_5 (.in(transistor_6_out), .out(transistor_3_out), .gate(c));
  Transistor #(.\type ("n")) transistor_6 (.in(transistor_7_out), .out(transistor_6_out), .gate(b));
  Transistor #(.\type ("n")) transistor_7 (.in(1'b0), .out(transistor_7_out), .gate(a));
  Transistor transistor_8 (.in(1'b1), .out(transistor_1_out), .gate(f));
  Transistor transistor_9 (.in(transistor_1_out), .out(transistor_3_out), .gate(c));
  Transistor #(.\type ("n")) transistor_10 (.in(transistor_11_out), .out(transistor_3_out), .gate(d));
  Transistor #(.\type ("n")) transistor_11 (.in(transistor_12_out), .out(transistor_11_out), .gate(e));
  Transistor #(.\type ("n")) transistor_12 (.in(1'b0), .out(transistor_12_out), .gate(f));
  Transistor transistor_13 (.in(1'b1), .out(g), .gate(transistor_3_out));
  Transistor #(.\type ("n")) transistor_14 (.in(1'b0), .out(g), .gate(transistor_3_out));
endmodule

module cell65 (
  input  nc1,
  input  nc2,
  input  c,
  input  a,
  input  b,
  input  c1,
  input  c2,
  output s,
  output ns,
  output c_out
);

  wire transistor_1_out, transistor_2_out, transistor_4_out, transistor_7_out, transistor_8_out,
       transistor_11_out, transistor_12_out, transistor_14_out, transistor_19_out, transistor_20_out,
       transistor_23_out, transistor_24_out, transistor_25_out, transistor_26_out, transistor_28_out,
       transistor_31_out, transistor_32_out, transistor_34_out;

  Transistor transistor_1 (.in(1'b1), .out(transistor_1_out), .gate(a));
  Transistor transistor_2 (.in(transistor_1_out), .out(transistor_2_out), .gate(c));
  Transistor #(.\type ("n")) transistor_3 (.in(transistor_4_out), .out(transistor_2_out), .gate(c));
  Transistor #(.\type ("n")) transistor_4 (.in(1'b0), .out(transistor_4_out), .gate(a));
  Transistor transistor_5 (.in(1'b1), .out(transistor_1_out), .gate(b));
  Transistor #(.\type ("n")) transistor_6 (.in(1'b0), .out(transistor_4_out), .gate(b));
  Transistor transistor_7 (.in(1'b1), .out(transistor_7_out), .gate(c));
  Transistor transistor_8 (.in(1'b1), .out(transistor_8_out), .gate(b));
  Transistor transistor_9 (.in(transistor_8_out), .out(transistor_2_out), .gate(a));
  Transistor #(.\type ("n")) transistor_10 (.in(transistor_11_out), .out(transistor_2_out), .gate(a));
  Transistor #(.\type ("n")) transistor_11 (.in(1'b0), .out(transistor_11_out), .gate(b));
  Transistor #(.\type ("n")) transistor_12 (.in(1'b0), .out(transistor_12_out), .gate(c));
  Transistor transistor_13 (.in(1'b1), .out(transistor_7_out), .gate(a));
  Transistor transistor_14 (.in(transistor_7_out), .out(transistor_14_out), .gate(transistor_2_out));
  Transistor #(.\type ("n")) transistor_15 (.in(transistor_12_out), .out(transistor_14_out), .gate(transistor_2_out));
  Transistor #(.\type ("n")) transistor_16 (.in(1'b0), .out(transistor_12_out), .gate(a));
  Transistor transistor_17 (.in(1'b1), .out(transistor_7_out), .gate(b));
  Transistor #(.\type ("n")) transistor_18 (.in(1'b0), .out(transistor_12_out), .gate(b));
  Transistor transistor_19 (.in(1'b1), .out(transistor_19_out), .gate(b));
  Transistor transistor_20 (.in(transistor_19_out), .out(transistor_20_out), .gate(a));
  Transistor transistor_21 (.in(transistor_20_out), .out(transistor_14_out), .gate(c));
  Transistor #(.\type ("n")) transistor_22 (.in(transistor_23_out), .out(transistor_14_out), .gate(c));
  Transistor #(.\type ("n")) transistor_23 (.in(transistor_24_out), .out(transistor_23_out), .gate(a));
  Transistor #(.\type ("n")) transistor_24 (.in(1'b0), .out(transistor_24_out), .gate(b));
  Transistor transistor_25 (.in(1'b1), .out(transistor_25_out), .gate(transistor_14_out));
  Transistor transistor_26 (.in(transistor_25_out), .out(transistor_26_out), .gate(nc1));
  Transistor #(.\type ("n")) transistor_27 (.in(transistor_28_out), .out(transistor_26_out), .gate(c1));
  Transistor #(.\type ("n")) transistor_28 (.in(1'b0), .out(transistor_28_out), .gate(transistor_14_out));
  Transistor transistor_29 (.in(1'b1), .out(c_out), .gate(transistor_2_out));
  Transistor #(.\type ("n")) transistor_30 (.in(1'b0), .out(c_out), .gate(transistor_2_out));
  Transistor transistor_31 (.in(1'b1), .out(transistor_31_out), .gate(transistor_26_out));
  Transistor transistor_32 (.in(transistor_31_out), .out(transistor_32_out), .gate(nc2));
  Transistor #(.\type ("n")) transistor_33 (.in(transistor_34_out), .out(transistor_32_out), .gate(c2));
  Transistor #(.\type ("n")) transistor_34 (.in(1'b0), .out(transistor_34_out), .gate(transistor_26_out));
  Transistor transistor_35 (.in(1'b1), .out(s), .gate(transistor_32_out));
  Transistor #(.\type ("n")) transistor_36 (.in(1'b0), .out(s), .gate(transistor_32_out));
  Transistor transistor_37 (.in(1'b1), .out(ns), .gate(s));
  Transistor #(.\type ("n")) transistor_38 (.in(1'b0), .out(ns), .gate(s));
endmodule

module cell66 (
  input  a,
  input  b,
  input  c,
  input  d,
  input  e,
  input  f,
  output g
);

  wire transistor_1_out, transistor_2_out, transistor_5_out, transistor_11_out, transistor_12_out;

  Transistor transistor_1 (.in(1'b1), .out(transistor_1_out), .gate(b));
  Transistor transistor_2 (.in(transistor_1_out), .out(transistor_2_out), .gate(c));
  Transistor transistor_3 (.in(transistor_2_out), .out(g), .gate(e));
  Transistor #(.\type ("n")) transistor_4 (.in(transistor_5_out), .out(g), .gate(a));
  Transistor #(.\type ("n")) transistor_5 (.in(1'b0), .out(transistor_5_out), .gate(b));
  Transistor transistor_6 (.in(1'b1), .out(transistor_1_out), .gate(a));
  Transistor transistor_7 (.in(transistor_1_out), .out(transistor_2_out), .gate(d));
  Transistor transistor_8 (.in(transistor_2_out), .out(g), .gate(f));
  Transistor #(.\type ("n")) transistor_9 (.in(transistor_11_out), .out(g), .gate(d));
  Transistor #(.\type ("n")) transistor_10 (.in(transistor_12_out), .out(g), .gate(e));
  Transistor #(.\type ("n")) transistor_11 (.in(1'b0), .out(transistor_11_out), .gate(c));
  Transistor #(.\type ("n")) transistor_12 (.in(1'b0), .out(transistor_12_out), .gate(f));
endmodule

module cell67 (
  input  b,
  input  c,
  input  d,
  input  e,
  input  f,
  input  g,
  input  h,
  input  i,
  output j
);

  wire transistor_1_out, transistor_2_out, transistor_3_out, transistor_4_out, transistor_7_out,
       transistor_8_out, transistor_9_out, transistor_10_out, transistor_20_out;

  Transistor transistor_1 (.in(1'b1), .out(transistor_1_out), .gate(b));
  Transistor transistor_2 (.in(transistor_1_out), .out(transistor_2_out), .gate(c));
  Transistor transistor_3 (.in(transistor_2_out), .out(transistor_3_out), .gate(d));
  Transistor transistor_4 (.in(transistor_3_out), .out(transistor_4_out), .gate(e));
  Transistor #(.\type ("n")) transistor_5 (.in(1'b0), .out(transistor_4_out), .gate(c));
  Transistor #(.\type ("n")) transistor_6 (.in(1'b0), .out(transistor_4_out), .gate(b));
  Transistor transistor_7 (.in(1'b1), .out(transistor_7_out), .gate(f));
  Transistor transistor_8 (.in(transistor_7_out), .out(transistor_8_out), .gate(g));
  Transistor transistor_9 (.in(transistor_8_out), .out(transistor_9_out), .gate(h));
  Transistor transistor_10 (.in(transistor_9_out), .out(transistor_10_out), .gate(i));
  Transistor #(.\type ("n")) transistor_11 (.in(1'b0), .out(transistor_10_out), .gate(g));
  Transistor #(.\type ("n")) transistor_12 (.in(1'b0), .out(transistor_10_out), .gate(f));
  Transistor #(.\type ("n")) transistor_13 (.in(1'b0), .out(transistor_4_out), .gate(d));
  Transistor #(.\type ("n")) transistor_14 (.in(1'b0), .out(transistor_4_out), .gate(e));
  Transistor #(.\type ("n")) transistor_15 (.in(1'b0), .out(transistor_10_out), .gate(i));
  Transistor #(.\type ("n")) transistor_16 (.in(1'b0), .out(transistor_10_out), .gate(h));
  Transistor transistor_17 (.in(1'b1), .out(j), .gate(transistor_10_out));
  Transistor transistor_18 (.in(1'b1), .out(j), .gate(transistor_4_out));
  Transistor #(.\type ("n")) transistor_19 (.in(transistor_20_out), .out(j), .gate(transistor_4_out));
  Transistor #(.\type ("n")) transistor_20 (.in(1'b0), .out(transistor_20_out), .gate(transistor_10_out));
endmodule

module cell68 (
  input  a,
  input  b,
  input  c,
  input  d,
  input  e,
  input  f,
  input  g,
  output h
);

  wire transistor_1_out, transistor_3_out, transistor_4_out, transistor_5_out, transistor_6_out,
       transistor_9_out, transistor_10_out, transistor_18_out;

  Transistor #(.\type ("n")) transistor_1 (.in(1'b0), .out(transistor_1_out), .gate(b));
  Transistor #(.\type ("n")) transistor_2 (.in(1'b0), .out(transistor_1_out), .gate(a));
  Transistor transistor_3 (.in(1'b1), .out(transistor_3_out), .gate(d));
  Transistor transistor_4 (.in(transistor_3_out), .out(transistor_4_out), .gate(e));
  Transistor transistor_5 (.in(transistor_4_out), .out(transistor_5_out), .gate(f));
  Transistor transistor_6 (.in(transistor_5_out), .out(transistor_6_out), .gate(g));
  Transistor #(.\type ("n")) transistor_7 (.in(1'b0), .out(transistor_6_out), .gate(e));
  Transistor #(.\type ("n")) transistor_8 (.in(1'b0), .out(transistor_6_out), .gate(d));
  Transistor transistor_9 (.in(1'b1), .out(transistor_9_out), .gate(c));
  Transistor transistor_10 (.in(transistor_9_out), .out(transistor_10_out), .gate(b));
  Transistor transistor_11 (.in(transistor_10_out), .out(transistor_1_out), .gate(a));
  Transistor #(.\type ("n")) transistor_12 (.in(1'b0), .out(transistor_1_out), .gate(c));
  Transistor #(.\type ("n")) transistor_13 (.in(1'b0), .out(transistor_6_out), .gate(f));
  Transistor #(.\type ("n")) transistor_14 (.in(1'b0), .out(transistor_6_out), .gate(g));
  Transistor transistor_15 (.in(1'b1), .out(h), .gate(transistor_6_out));
  Transistor transistor_16 (.in(1'b1), .out(h), .gate(transistor_1_out));
  Transistor #(.\type ("n")) transistor_17 (.in(transistor_18_out), .out(h), .gate(transistor_1_out));
  Transistor #(.\type ("n")) transistor_18 (.in(1'b0), .out(transistor_18_out), .gate(transistor_6_out));
endmodule

module cell69 (
  input  b,
  input  c,
  input  d,
  input  e,
  input  f,
  input  g,
  input  h,
  output a
);

  wire transistor_1_out, transistor_4_out, transistor_5_out, transistor_6_out, transistor_7_out,
       transistor_13_out, transistor_14_out, transistor_15_out, transistor_16_out;

  Transistor transistor_1 (.in(1'b1), .out(transistor_1_out), .gate(e));
  Transistor transistor_2 (.in(1'b1), .out(transistor_1_out), .gate(d));
  Transistor #(.\type ("n")) transistor_3 (.in(transistor_4_out), .out(transistor_1_out), .gate(b));
  Transistor #(.\type ("n")) transistor_4 (.in(transistor_5_out), .out(transistor_4_out), .gate(c));
  Transistor #(.\type ("n")) transistor_5 (.in(transistor_6_out), .out(transistor_5_out), .gate(d));
  Transistor #(.\type ("n")) transistor_6 (.in(1'b0), .out(transistor_6_out), .gate(e));
  Transistor transistor_7 (.in(1'b1), .out(transistor_7_out), .gate(h));
  Transistor transistor_8 (.in(1'b1), .out(transistor_7_out), .gate(g));
  Transistor transistor_9 (.in(1'b1), .out(transistor_1_out), .gate(c));
  Transistor transistor_10 (.in(1'b1), .out(transistor_1_out), .gate(b));
  Transistor transistor_11 (.in(1'b1), .out(transistor_7_out), .gate(f));
  Transistor #(.\type ("n")) transistor_12 (.in(transistor_13_out), .out(transistor_7_out), .gate(h));
  Transistor #(.\type ("n")) transistor_13 (.in(transistor_14_out), .out(transistor_13_out), .gate(g));
  Transistor #(.\type ("n")) transistor_14 (.in(1'b0), .out(transistor_14_out), .gate(f));
  Transistor transistor_15 (.in(1'b1), .out(transistor_15_out), .gate(transistor_7_out));
  Transistor transistor_16 (.in(transistor_15_out), .out(transistor_16_out), .gate(transistor_1_out));
  Transistor #(.\type ("n")) transistor_17 (.in(1'b0), .out(transistor_16_out), .gate(transistor_1_out));
  Transistor #(.\type ("n")) transistor_18 (.in(1'b0), .out(transistor_16_out), .gate(transistor_7_out));
  Transistor transistor_19 (.in(1'b1), .out(a), .gate(transistor_16_out));
  Transistor #(.\type ("n")) transistor_20 (.in(1'b0), .out(a), .gate(transistor_16_out));
endmodule

module cell70 (
  input  a,
  input  b,
  input  c,
  output e,
  output d
);

  wire transistor_1_out, transistor_2_out, transistor_4_out, transistor_5_out, transistor_6_out,
       transistor_8_out, transistor_14_out, transistor_18_out;

  Transistor transistor_1 (.in(1'b1), .out(transistor_1_out), .gate(transistor_6_out));
  Transistor transistor_2 (.in(transistor_1_out), .out(transistor_2_out), .gate(a));
  Transistor #(.\type ("n")) transistor_3 (.in(transistor_4_out), .out(transistor_2_out), .gate(b));
  Transistor #(.\type ("n")) transistor_4 (.in(1'b0), .out(transistor_4_out), .gate(a));
  Transistor transistor_5 (.in(1'b1), .out(transistor_5_out), .gate(transistor_2_out));
  Transistor transistor_6 (.in(transistor_5_out), .out(transistor_6_out), .gate(c));
  Transistor #(.\type ("n")) transistor_7 (.in(transistor_8_out), .out(transistor_6_out), .gate(b));
  Transistor #(.\type ("n")) transistor_8 (.in(1'b0), .out(transistor_8_out), .gate(c));
  Transistor transistor_9 (.in(transistor_1_out), .out(transistor_2_out), .gate(b));
  Transistor #(.\type ("n")) transistor_10 (.in(1'b0), .out(transistor_2_out), .gate(transistor_6_out));
  Transistor transistor_11 (.in(transistor_5_out), .out(transistor_6_out), .gate(b));
  Transistor #(.\type ("n")) transistor_12 (.in(1'b0), .out(transistor_6_out), .gate(transistor_2_out));
  Transistor transistor_13 (.in(1'b1), .out(e), .gate(transistor_14_out));
  Transistor transistor_14 (.in(1'b1), .out(transistor_14_out), .gate(transistor_2_out));
  Transistor #(.\type ("n")) transistor_15 (.in(1'b0), .out(transistor_14_out), .gate(transistor_2_out));
  Transistor #(.\type ("n")) transistor_16 (.in(1'b0), .out(e), .gate(transistor_14_out));
  Transistor transistor_17 (.in(1'b1), .out(d), .gate(transistor_18_out));
  Transistor transistor_18 (.in(1'b1), .out(transistor_18_out), .gate(transistor_6_out));
  Transistor #(.\type ("n")) transistor_19 (.in(1'b0), .out(transistor_18_out), .gate(transistor_6_out));
  Transistor #(.\type ("n")) transistor_20 (.in(1'b0), .out(d), .gate(transistor_18_out));
endmodule

module cell71 (
  input  a,
  input  b,
  output d,
  output e
);

  wire transistor_1_out, transistor_2_out, transistor_4_out, transistor_5_out, transistor_10_out,
       transistor_13_out;

  Transistor transistor_1 (.in(1'b1), .out(transistor_1_out), .gate(transistor_5_out));
  Transistor transistor_2 (.in(transistor_1_out), .out(transistor_2_out), .gate(a));
  Transistor #(.\type ("n")) transistor_3 (.in(1'b0), .out(transistor_2_out), .gate(a));
  Transistor transistor_4 (.in(1'b1), .out(transistor_4_out), .gate(transistor_2_out));
  Transistor transistor_5 (.in(transistor_4_out), .out(transistor_5_out), .gate(b));
  Transistor #(.\type ("n")) transistor_6 (.in(1'b0), .out(transistor_5_out), .gate(b));
  Transistor #(.\type ("n")) transistor_7 (.in(1'b0), .out(transistor_2_out), .gate(transistor_5_out));
  Transistor #(.\type ("n")) transistor_8 (.in(1'b0), .out(transistor_5_out), .gate(transistor_2_out));
  Transistor transistor_9 (.in(1'b1), .out(d), .gate(transistor_10_out));
  Transistor transistor_10 (.in(1'b1), .out(transistor_10_out), .gate(transistor_2_out));
  Transistor #(.\type ("n")) transistor_11 (.in(1'b0), .out(d), .gate(transistor_10_out));
  Transistor #(.\type ("n")) transistor_12 (.in(1'b0), .out(transistor_10_out), .gate(transistor_2_out));
  Transistor transistor_13 (.in(1'b1), .out(transistor_13_out), .gate(transistor_5_out));
  Transistor transistor_14 (.in(1'b1), .out(e), .gate(transistor_13_out));
  Transistor #(.\type ("n")) transistor_15 (.in(1'b0), .out(e), .gate(transistor_13_out));
  Transistor #(.\type ("n")) transistor_16 (.in(1'b0), .out(transistor_13_out), .gate(transistor_5_out));
endmodule

module cell73 (
  input  a,
  input  b,
  input  c,
  input  d,
  output e
);

  wire transistor_4_out, transistor_5_out, transistor_7_out;

  Transistor transistor_1 (.in(1'b1), .out(e), .gate(c));
  Transistor transistor_2 (.in(1'b1), .out(e), .gate(d));
  Transistor #(.\type ("n")) transistor_3 (.in(transistor_4_out), .out(e), .gate(d));
  Transistor #(.\type ("n")) transistor_4 (.in(transistor_5_out), .out(transistor_4_out), .gate(c));
  Transistor #(.\type ("n")) transistor_5 (.in(1'b0), .out(transistor_5_out), .gate(b));
  Transistor #(.\type ("n")) transistor_6 (.in(1'b0), .out(transistor_5_out), .gate(a));
  Transistor transistor_7 (.in(1'b1), .out(transistor_7_out), .gate(a));
  Transistor transistor_8 (.in(transistor_7_out), .out(e), .gate(b));
endmodule

module cell74 (
  input  a,
  input  c,
  output out_3
);

  wire transistor_1_out, transistor_3_out, transistor_5_out, transistor_8_out;

  Transistor transistor_1 (.in(1'b1), .out(transistor_1_out), .gate(a));
  Transistor #(.\type ("n")) transistor_2 (.in(1'b0), .out(transistor_1_out), .gate(a));
  Transistor transistor_3 (.in(1'b1), .out(transistor_3_out), .gate(c));
  Transistor #(.\type ("n")) transistor_4 (.in(1'b0), .out(transistor_3_out), .gate(c));
  Transistor transistor_5 (.in(1'b1), .out(transistor_5_out), .gate(transistor_3_out));
  Transistor transistor_6 (.in(transistor_5_out), .out(out_3), .gate(a));
  Transistor #(.\type ("n")) transistor_7 (.in(transistor_8_out), .out(out_3), .gate(transistor_1_out));
  Transistor #(.\type ("n")) transistor_8 (.in(1'b0), .out(transistor_8_out), .gate(transistor_3_out));
endmodule

module cell75 (
  input  a,
  input  b,
  input  c,
  input  d,
  output e
);

  wire transistor_1_out, transistor_2_out, transistor_4_out, transistor_5_out, transistor_8_out,
       transistor_9_out, transistor_10_out, transistor_13_out;

  Transistor transistor_1 (.in(1'b1), .out(transistor_1_out), .gate(a));
  Transistor transistor_2 (.in(transistor_1_out), .out(transistor_2_out), .gate(c));
  Transistor #(.\type ("n")) transistor_3 (.in(transistor_4_out), .out(transistor_2_out), .gate(b));
  Transistor #(.\type ("n")) transistor_4 (.in(1'b0), .out(transistor_4_out), .gate(a));
  Transistor transistor_5 (.in(1'b1), .out(transistor_5_out), .gate(transistor_10_out));
  Transistor transistor_6 (.in(transistor_5_out), .out(transistor_2_out), .gate(b));
  Transistor #(.\type ("n")) transistor_7 (.in(transistor_8_out), .out(transistor_2_out), .gate(c));
  Transistor #(.\type ("n")) transistor_8 (.in(1'b0), .out(transistor_8_out), .gate(transistor_10_out));
  Transistor transistor_9 (.in(1'b1), .out(transistor_9_out), .gate(transistor_2_out));
  Transistor transistor_10 (.in(transistor_9_out), .out(transistor_10_out), .gate(d));
  Transistor #(.\type ("n")) transistor_11 (.in(1'b0), .out(transistor_10_out), .gate(d));
  Transistor #(.\type ("n")) transistor_12 (.in(1'b0), .out(transistor_10_out), .gate(transistor_2_out));
  Transistor transistor_13 (.in(1'b1), .out(transistor_13_out), .gate(transistor_10_out));
  Transistor #(.\type ("n")) transistor_14 (.in(1'b0), .out(transistor_13_out), .gate(transistor_10_out));
  Transistor transistor_15 (.in(1'b1), .out(e), .gate(transistor_13_out));
  Transistor #(.\type ("n")) transistor_16 (.in(1'b0), .out(e), .gate(transistor_13_out));
endmodule

module cell76 (
  input  nc1,
  input  nc2,
  input  c_in,
  input  r,
  input  c2,
  input  c1,
  input  a,
  output c_out,
  output ns,
  output s
);

  wire transistor_1_out, transistor_4_out, transistor_7_out, transistor_8_out, transistor_9_out,
       transistor_11_out, transistor_12_out, transistor_16_out, transistor_17_out, transistor_18_out,
       transistor_20_out, transistor_21_out, transistor_22_out, transistor_24_out, transistor_25_out,
       transistor_26_out;

  Transistor transistor_1 (.in(1'b1), .out(transistor_1_out), .gate(c_in));
  Transistor #(.\type ("n")) transistor_2 (.in(1'b0), .out(transistor_1_out), .gate(c_in));
  Transistor #(.\type ("n")) transistor_3 (.in(1'b0), .out(c_out), .gate(transistor_1_out));
  Transistor transistor_4 (.in(1'b1), .out(transistor_4_out), .gate(transistor_26_out));
  Transistor transistor_5 (.in(transistor_4_out), .out(c_out), .gate(transistor_1_out));
  Transistor #(.\type ("n")) transistor_6 (.in(1'b0), .out(c_out), .gate(transistor_26_out));
  Transistor transistor_7 (.in(1'b1), .out(transistor_7_out), .gate(transistor_1_out));
  Transistor transistor_8 (.in(transistor_7_out), .out(transistor_8_out), .gate(c_out));
  Transistor transistor_9 (.in(transistor_8_out), .out(transistor_9_out), .gate(r));
  Transistor #(.\type ("n")) transistor_10 (.in(1'b0), .out(transistor_9_out), .gate(r));
  Transistor transistor_11 (.in(1'b1), .out(transistor_11_out), .gate(c_out));
  Transistor transistor_12 (.in(transistor_11_out), .out(transistor_12_out), .gate(transistor_26_out));
  Transistor transistor_13 (.in(transistor_12_out), .out(transistor_9_out), .gate(r));
  Transistor #(.\type ("n")) transistor_14 (.in(1'b0), .out(transistor_9_out), .gate(c_out));
  Transistor #(.\type ("n")) transistor_15 (.in(transistor_16_out), .out(transistor_9_out), .gate(transistor_26_out));
  Transistor #(.\type ("n")) transistor_16 (.in(1'b0), .out(transistor_16_out), .gate(transistor_1_out));
  Transistor transistor_17 (.in(1'b1), .out(transistor_17_out), .gate(transistor_9_out));
  Transistor transistor_18 (.in(transistor_17_out), .out(transistor_18_out), .gate(nc1));
  Transistor #(.\type ("n")) transistor_19 (.in(transistor_20_out), .out(transistor_18_out), .gate(c1));
  Transistor #(.\type ("n")) transistor_20 (.in(1'b0), .out(transistor_20_out), .gate(transistor_9_out));
  Transistor transistor_21 (.in(1'b1), .out(transistor_21_out), .gate(transistor_18_out));
  Transistor transistor_22 (.in(transistor_21_out), .out(transistor_22_out), .gate(nc2));
  Transistor #(.\type ("n")) transistor_23 (.in(transistor_24_out), .out(transistor_22_out), .gate(c2));
  Transistor #(.\type ("n")) transistor_24 (.in(1'b0), .out(transistor_24_out), .gate(transistor_18_out));
  Transistor transistor_25 (.in(1'b1), .out(transistor_25_out), .gate(a));
  Transistor transistor_26 (.in(transistor_25_out), .out(transistor_26_out), .gate(transistor_22_out));
  Transistor #(.\type ("n")) transistor_27 (.in(1'b0), .out(transistor_26_out), .gate(transistor_22_out));
  Transistor #(.\type ("n")) transistor_28 (.in(1'b0), .out(transistor_26_out), .gate(a));
  Transistor transistor_29 (.in(1'b1), .out(s), .gate(transistor_26_out));
  Transistor #(.\type ("n")) transistor_30 (.in(1'b0), .out(s), .gate(transistor_26_out));
  Transistor transistor_31 (.in(1'b1), .out(ns), .gate(s));
  Transistor #(.\type ("n")) transistor_32 (.in(1'b0), .out(ns), .gate(s));
endmodule

module cell77 (
  input  r,
  input  nc1,
  input  nc2,
  input  c,
  input  a,
  input  c1,
  input  c2,
  output ns,
  output s,
  output c_out
);

  wire transistor_1_out, transistor_2_out, transistor_4_out, transistor_7_out, transistor_8_out,
       transistor_11_out, transistor_12_out, transistor_14_out, transistor_19_out, transistor_20_out,
       transistor_23_out, transistor_24_out, transistor_25_out, transistor_26_out, transistor_31_out,
       transistor_32_out, transistor_34_out, transistor_35_out, transistor_36_out, transistor_38_out;

  Transistor transistor_1 (.in(1'b1), .out(transistor_1_out), .gate(a));
  Transistor transistor_2 (.in(transistor_1_out), .out(transistor_2_out), .gate(c));
  Transistor #(.\type ("n")) transistor_3 (.in(transistor_4_out), .out(transistor_2_out), .gate(c));
  Transistor #(.\type ("n")) transistor_4 (.in(1'b0), .out(transistor_4_out), .gate(a));
  Transistor transistor_5 (.in(1'b1), .out(transistor_1_out), .gate(transistor_36_out));
  Transistor #(.\type ("n")) transistor_6 (.in(1'b0), .out(transistor_4_out), .gate(transistor_36_out));
  Transistor transistor_7 (.in(1'b1), .out(transistor_7_out), .gate(c));
  Transistor transistor_8 (.in(1'b1), .out(transistor_8_out), .gate(transistor_36_out));
  Transistor transistor_9 (.in(transistor_8_out), .out(transistor_2_out), .gate(a));
  Transistor #(.\type ("n")) transistor_10 (.in(transistor_11_out), .out(transistor_2_out), .gate(a));
  Transistor #(.\type ("n")) transistor_11 (.in(1'b0), .out(transistor_11_out), .gate(transistor_36_out));
  Transistor #(.\type ("n")) transistor_12 (.in(1'b0), .out(transistor_12_out), .gate(c));
  Transistor transistor_13 (.in(1'b1), .out(transistor_7_out), .gate(a));
  Transistor transistor_14 (.in(transistor_7_out), .out(transistor_14_out), .gate(transistor_2_out));
  Transistor #(.\type ("n")) transistor_15 (.in(transistor_12_out), .out(transistor_14_out), .gate(transistor_2_out));
  Transistor #(.\type ("n")) transistor_16 (.in(1'b0), .out(transistor_12_out), .gate(a));
  Transistor transistor_17 (.in(1'b1), .out(transistor_7_out), .gate(transistor_36_out));
  Transistor #(.\type ("n")) transistor_18 (.in(1'b0), .out(transistor_12_out), .gate(transistor_36_out));
  Transistor transistor_19 (.in(1'b1), .out(transistor_19_out), .gate(transistor_36_out));
  Transistor transistor_20 (.in(transistor_19_out), .out(transistor_20_out), .gate(a));
  Transistor transistor_21 (.in(transistor_20_out), .out(transistor_14_out), .gate(c));
  Transistor #(.\type ("n")) transistor_22 (.in(transistor_23_out), .out(transistor_14_out), .gate(c));
  Transistor #(.\type ("n")) transistor_23 (.in(transistor_24_out), .out(transistor_23_out), .gate(a));
  Transistor #(.\type ("n")) transistor_24 (.in(1'b0), .out(transistor_24_out), .gate(transistor_36_out));
  Transistor transistor_25 (.in(1'b1), .out(transistor_25_out), .gate(r));
  Transistor transistor_26 (.in(transistor_25_out), .out(transistor_26_out), .gate(transistor_14_out));
  Transistor #(.\type ("n")) transistor_27 (.in(1'b0), .out(transistor_26_out), .gate(r));
  Transistor transistor_28 (.in(1'b1), .out(c_out), .gate(transistor_2_out));
  Transistor #(.\type ("n")) transistor_29 (.in(1'b0), .out(c_out), .gate(transistor_2_out));
  Transistor #(.\type ("n")) transistor_30 (.in(1'b0), .out(transistor_26_out), .gate(transistor_14_out));
  Transistor transistor_31 (.in(1'b1), .out(transistor_31_out), .gate(transistor_26_out));
  Transistor transistor_32 (.in(transistor_31_out), .out(transistor_32_out), .gate(nc1));
  Transistor #(.\type ("n")) transistor_33 (.in(transistor_34_out), .out(transistor_32_out), .gate(c1));
  Transistor #(.\type ("n")) transistor_34 (.in(1'b0), .out(transistor_34_out), .gate(transistor_26_out));
  Transistor transistor_35 (.in(1'b1), .out(transistor_35_out), .gate(transistor_32_out));
  Transistor transistor_36 (.in(transistor_35_out), .out(transistor_36_out), .gate(nc2));
  Transistor #(.\type ("n")) transistor_37 (.in(transistor_38_out), .out(transistor_36_out), .gate(c2));
  Transistor #(.\type ("n")) transistor_38 (.in(1'b0), .out(transistor_38_out), .gate(transistor_32_out));
  Transistor transistor_39 (.in(1'b1), .out(ns), .gate(transistor_36_out));
  Transistor #(.\type ("n")) transistor_40 (.in(1'b0), .out(ns), .gate(transistor_36_out));
  Transistor transistor_41 (.in(1'b1), .out(s), .gate(ns));
  Transistor #(.\type ("n")) transistor_42 (.in(1'b0), .out(s), .gate(ns));
endmodule

module cell78 (
  input  a,
  input  b,
  input  c,
  input  d,
  input  e,
  input  f,
  input  g,
  input  h,
  input  i,
  output j
);

  wire transistor_1_out, transistor_2_out, transistor_3_out, transistor_5_out, transistor_6_out,
       transistor_11_out, transistor_12_out, transistor_17_out, transistor_18_out;

  Transistor transistor_1 (.in(1'b1), .out(transistor_1_out), .gate(g));
  Transistor transistor_2 (.in(transistor_1_out), .out(transistor_2_out), .gate(d));
  Transistor transistor_3 (.in(transistor_2_out), .out(transistor_3_out), .gate(a));
  Transistor #(.\type ("n")) transistor_4 (.in(transistor_5_out), .out(transistor_3_out), .gate(a));
  Transistor #(.\type ("n")) transistor_5 (.in(transistor_6_out), .out(transistor_5_out), .gate(b));
  Transistor #(.\type ("n")) transistor_6 (.in(1'b0), .out(transistor_6_out), .gate(c));
  Transistor transistor_7 (.in(1'b1), .out(transistor_1_out), .gate(h));
  Transistor transistor_8 (.in(transistor_1_out), .out(transistor_2_out), .gate(e));
  Transistor transistor_9 (.in(transistor_2_out), .out(transistor_3_out), .gate(b));
  Transistor #(.\type ("n")) transistor_10 (.in(transistor_11_out), .out(transistor_3_out), .gate(f));
  Transistor #(.\type ("n")) transistor_11 (.in(transistor_12_out), .out(transistor_11_out), .gate(e));
  Transistor #(.\type ("n")) transistor_12 (.in(1'b0), .out(transistor_12_out), .gate(d));
  Transistor transistor_13 (.in(1'b1), .out(transistor_1_out), .gate(i));
  Transistor transistor_14 (.in(transistor_1_out), .out(transistor_2_out), .gate(f));
  Transistor transistor_15 (.in(transistor_2_out), .out(transistor_3_out), .gate(c));
  Transistor #(.\type ("n")) transistor_16 (.in(transistor_17_out), .out(transistor_3_out), .gate(g));
  Transistor #(.\type ("n")) transistor_17 (.in(transistor_18_out), .out(transistor_17_out), .gate(h));
  Transistor #(.\type ("n")) transistor_18 (.in(1'b0), .out(transistor_18_out), .gate(i));
  Transistor transistor_19 (.in(1'b1), .out(j), .gate(transistor_3_out));
  Transistor #(.\type ("n")) transistor_20 (.in(1'b0), .out(j), .gate(transistor_3_out));
endmodule

module cell79 (
  input  a,
  input  b,
  input  c,
  input  d,
  input  e,
  input  f,
  input  h,
  input  i,
  input  j,
  output g
);

  wire transistor_1_out, transistor_2_out, transistor_3_out, transistor_4_out, transistor_7_out,
       transistor_8_out, transistor_9_out, transistor_12_out, transistor_13_out, transistor_22_out,
       transistor_23_out;

  Transistor #(.\type ("n")) transistor_1 (.in(1'b0), .out(transistor_1_out), .gate(a));
  Transistor transistor_2 (.in(1'b1), .out(transistor_2_out), .gate(d));
  Transistor transistor_3 (.in(transistor_2_out), .out(transistor_3_out), .gate(e));
  Transistor transistor_4 (.in(transistor_3_out), .out(transistor_4_out), .gate(f));
  Transistor #(.\type ("n")) transistor_5 (.in(1'b0), .out(transistor_4_out), .gate(e));
  Transistor #(.\type ("n")) transistor_6 (.in(1'b0), .out(transistor_4_out), .gate(d));
  Transistor transistor_7 (.in(1'b1), .out(transistor_7_out), .gate(h));
  Transistor transistor_8 (.in(transistor_7_out), .out(transistor_8_out), .gate(i));
  Transistor transistor_9 (.in(transistor_8_out), .out(transistor_9_out), .gate(j));
  Transistor #(.\type ("n")) transistor_10 (.in(1'b0), .out(transistor_9_out), .gate(i));
  Transistor #(.\type ("n")) transistor_11 (.in(1'b0), .out(transistor_9_out), .gate(h));
  Transistor transistor_12 (.in(1'b1), .out(transistor_12_out), .gate(c));
  Transistor transistor_13 (.in(transistor_12_out), .out(transistor_13_out), .gate(b));
  Transistor transistor_14 (.in(transistor_13_out), .out(transistor_1_out), .gate(a));
  Transistor #(.\type ("n")) transistor_15 (.in(1'b0), .out(transistor_1_out), .gate(c));
  Transistor #(.\type ("n")) transistor_16 (.in(1'b0), .out(transistor_1_out), .gate(b));
  Transistor #(.\type ("n")) transistor_17 (.in(1'b0), .out(transistor_4_out), .gate(f));
  Transistor #(.\type ("n")) transistor_18 (.in(1'b0), .out(transistor_9_out), .gate(j));
  Transistor transistor_19 (.in(1'b1), .out(g), .gate(transistor_4_out));
  Transistor transistor_20 (.in(1'b1), .out(g), .gate(transistor_1_out));
  Transistor #(.\type ("n")) transistor_21 (.in(transistor_22_out), .out(g), .gate(transistor_9_out));
  Transistor #(.\type ("n")) transistor_22 (.in(transistor_23_out), .out(transistor_22_out), .gate(transistor_1_out));
  Transistor #(.\type ("n")) transistor_23 (.in(1'b0), .out(transistor_23_out), .gate(transistor_4_out));
  Transistor transistor_24 (.in(1'b1), .out(g), .gate(transistor_9_out));
endmodule

module cell80 (
  input  b,
  input  c,
  input  d,
  input  e,
  input  f,
  input  g,
  input  h,
  input  i,
  output a
);

  wire transistor_1_out, transistor_2_out, transistor_3_out, transistor_4_out, transistor_7_out,
       transistor_8_out, transistor_9_out, transistor_10_out, transistor_17_out, transistor_20_out;

  Transistor transistor_1 (.in(1'b1), .out(transistor_1_out), .gate(b));
  Transistor transistor_2 (.in(transistor_1_out), .out(transistor_2_out), .gate(c));
  Transistor transistor_3 (.in(transistor_2_out), .out(transistor_3_out), .gate(d));
  Transistor transistor_4 (.in(transistor_3_out), .out(transistor_4_out), .gate(e));
  Transistor #(.\type ("n")) transistor_5 (.in(1'b0), .out(transistor_4_out), .gate(c));
  Transistor #(.\type ("n")) transistor_6 (.in(1'b0), .out(transistor_4_out), .gate(b));
  Transistor transistor_7 (.in(1'b1), .out(transistor_7_out), .gate(f));
  Transistor transistor_8 (.in(transistor_7_out), .out(transistor_8_out), .gate(g));
  Transistor transistor_9 (.in(transistor_8_out), .out(transistor_9_out), .gate(h));
  Transistor transistor_10 (.in(transistor_9_out), .out(transistor_10_out), .gate(i));
  Transistor #(.\type ("n")) transistor_11 (.in(1'b0), .out(transistor_10_out), .gate(f));
  Transistor #(.\type ("n")) transistor_12 (.in(1'b0), .out(transistor_10_out), .gate(g));
  Transistor #(.\type ("n")) transistor_13 (.in(1'b0), .out(transistor_4_out), .gate(d));
  Transistor #(.\type ("n")) transistor_14 (.in(1'b0), .out(transistor_4_out), .gate(e));
  Transistor #(.\type ("n")) transistor_15 (.in(1'b0), .out(transistor_10_out), .gate(i));
  Transistor #(.\type ("n")) transistor_16 (.in(1'b0), .out(transistor_10_out), .gate(h));
  Transistor transistor_17 (.in(1'b1), .out(transistor_17_out), .gate(transistor_10_out));
  Transistor transistor_18 (.in(1'b1), .out(transistor_17_out), .gate(transistor_4_out));
  Transistor #(.\type ("n")) transistor_19 (.in(transistor_20_out), .out(transistor_17_out), .gate(transistor_4_out));
  Transistor #(.\type ("n")) transistor_20 (.in(1'b0), .out(transistor_20_out), .gate(transistor_10_out));
  Transistor transistor_21 (.in(1'b1), .out(a), .gate(transistor_17_out));
  Transistor #(.\type ("n")) transistor_22 (.in(1'b0), .out(a), .gate(transistor_17_out));
endmodule
